// Logisim project 实验1.circ as structural Verilog: 5 circuits, main circuit 一位二进制全加器
module \一位二进制半加器  (
  input  A,
  input  B,
  output S,
  output C
);

  xor xor_1 (S, A, B);
  and and_1 (C, A, B);

  // Notes on the sheet:
  //   一位二进制半加器
endmodule

module \一位二进制全加器  (
  input  A,
  input  B,
  input  Ci,
  output S,
  output C0
);

  wire and_1_out, and_2_out, and_3_out, or_1_out, xor_1_out;

  and and_1 (and_1_out, A, B);
  and and_2 (and_2_out, B, Ci);
  xor xor_1 (xor_1_out, A, B);
  or or_1 (or_1_out, and_1_out, and_2_out);
  and and_3 (and_3_out, A, Ci);
  xor xor_2 (S, xor_1_out, Ci);
  or or_2 (C0, or_1_out, and_3_out);

  // Notes on the sheet:
  //   一位二进制全加器
endmodule

module \串行进位并行加法器  (
  input  C0,
  input  A3,
  input  B3,
  input  A2,
  input  B2,
  input  A1,
  input  B1,
  input  A0,
  input  B0,
  output S3,
  output S2,
  output S1,
  output S0,
  output C
);

  wire \一位二进制全加器_2_c0 , \一位二进制全加器_3_c0 , \一位二进制全加器_4_c0 ;

  \一位二进制全加器  \u_一位二进制全加器_1  (.A(A3), .B(B3), .Ci(\一位二进制全加器_2_c0 ), .S(S3), .C0(C));
  \一位二进制全加器  \u_一位二进制全加器_2  (.A(A2), .B(B2), .Ci(\一位二进制全加器_3_c0 ), .S(S2), .C0(\一位二进制全加器_2_c0 ));
  \一位二进制全加器  \u_一位二进制全加器_3  (.A(A1), .B(B1), .Ci(\一位二进制全加器_4_c0 ), .S(S1), .C0(\一位二进制全加器_3_c0 ));
  \一位二进制全加器  \u_一位二进制全加器_4  (.A(A0), .B(B0), .Ci(C0), .S(S0), .C0(\一位二进制全加器_4_c0 ));

  // Notes on the sheet:
  //   串行进位的四位二进制并行加法器
endmodule

module \先行进位并行加法器  (
  input  A0,
  input  A1,
  input  A2,
  input  A3,
  input  B0,
  input  B1,
  input  B2,
  input  B3,
  input  C0,
  output S0,
  output S1,
  output S2,
  output S3,
  output C4
);

  wire and_1_out, and_2_out, and_3_out, and_4_out, and_5_out, and_6_out, and_7_out, and_8_out, and_9_out,
       and_10_out, and_11_out, and_12_out, and_13_out, and_14_out, or_1_out, or_2_out, or_3_out, xor_1_out,
       xor_2_out, xor_3_out, xor_4_out, xor_5_out, xor_6_out, xor_7_out, xor_8_out, xor_9_out, xor_10_out,
       xor_11_out, xor_12_out, xor_13_out, xor_14_out, xor_15_out, xor_16_out, xor_17_out, xor_18_out,
       xor_19_out, xor_20_out;

  xor xor_1 (xor_1_out, A0, B0);
  xor xor_2 (xor_2_out, A1, B1);
  xor xor_3 (xor_3_out, A0, B0);
  xor xor_4 (xor_4_out, A1, B1);
  xor xor_5 (xor_5_out, A2, B2);
  xor xor_6 (xor_6_out, A1, B1);
  xor xor_7 (xor_7_out, A0, B0);
  xor xor_8 (xor_8_out, A2, B2);
  xor xor_9 (xor_9_out, A1, B1);
  xor xor_10 (xor_10_out, A2, B2);
  xor xor_11 (xor_11_out, A3, B3);
  xor xor_12 (xor_12_out, A2, B2);
  xor xor_13 (xor_13_out, A1, B1);
  xor xor_14 (xor_14_out, A0, B0);
  xor xor_15 (xor_15_out, A3, B3);
  xor xor_16 (xor_16_out, A2, B2);
  xor xor_17 (xor_17_out, A1, B1);
  xor xor_18 (xor_18_out, A3, B3);
  xor xor_19 (xor_19_out, A2, B2);
  xor xor_20 (xor_20_out, A3, B3);
  xor xor_21 (S0, A0, B0, C0);
  and and_1 (and_1_out, xor_1_out, C0);
  and and_2 (and_2_out, A0, B0);
  and and_3 (and_3_out, xor_2_out, xor_3_out, C0);
  and and_4 (and_4_out, A0, B0, xor_4_out);
  and and_5 (and_5_out, A1, B1);
  and and_6 (and_6_out, xor_5_out, xor_6_out, xor_7_out, C0);
  and and_7 (and_7_out, xor_8_out, xor_9_out, A0, B0);
  and and_8 (and_8_out, A1, B1, xor_10_out);
  and and_9 (and_9_out, A2, B2);
  and and_10 (and_10_out, xor_11_out, xor_12_out, xor_13_out, xor_14_out, C0);
  and and_11 (and_11_out, xor_15_out, xor_16_out, xor_17_out, A0, B0);
  and and_12 (and_12_out, xor_18_out, xor_19_out, A1, B1);
  and and_13 (and_13_out, A2, B2, xor_20_out);
  and and_14 (and_14_out, A3, B3);
  or or_1 (or_1_out, and_1_out, and_2_out);
  or or_2 (or_2_out, and_3_out, and_4_out, and_5_out);
  or or_3 (or_3_out, and_6_out, and_7_out, and_8_out, and_9_out);
  or or_4 (C4, and_10_out, and_11_out, and_12_out, and_13_out, and_14_out);
  xor xor_22 (S1, A1, B1, or_1_out);
  xor xor_23 (S2, A2, B2, or_2_out);
  xor xor_24 (S3, A3, B3, or_3_out);
endmodule

module \先行进位并行加法器测试电路  (
  input  in_1,
  input  in_2,
  input  in_3,
  input  in_4,
  input  in_5,
  input  in_6,
  input  in_7,
  input  in_8,
  input  in_9,
  output out_10,
  output out_11,
  output out_12,
  output out_13,
  output out_14
);

  \先行进位并行加法器  \u_先行进位并行加法器_1  (
    .A0(in_8), .A1(in_6), .A2(in_4), .A3(in_2), .B0(in_3), .B1(in_5), .B2(in_7), .B3(in_9), .C0(in_1),
    .S0(out_13), .S1(out_12), .S2(out_11), .S3(out_10), .C4(out_14));
endmodule
