// Logisim project 实验2.circ as structural Verilog: 14 circuits, main circuit 一位二进制全加器
module \一位二进制半加器  (
  input  A,
  input  B,
  output S,
  output C
);

  xor xor_1 (S, A, B);
  and and_1 (C, A, B);

  // Notes on the sheet:
  //   一位二进制半加器
endmodule

module \一位二进制全加器  (
  input  A,
  input  B,
  input  Ci,
  output S,
  output C0
);

  wire and_1_out, and_2_out, and_3_out, or_1_out, xor_1_out;

  and and_1 (and_1_out, A, B);
  and and_2 (and_2_out, B, Ci);
  xor xor_1 (xor_1_out, A, B);
  or or_1 (or_1_out, and_1_out, and_2_out);
  and and_3 (and_3_out, A, Ci);
  xor xor_2 (S, xor_1_out, Ci);
  or or_2 (C0, or_1_out, and_3_out);

  // Notes on the sheet:
  //   一位二进制全加器
endmodule

module \串行进位并行加法器  (
  input  C0,
  input  A3,
  input  B3,
  input  A2,
  input  B2,
  input  A1,
  input  B1,
  input  A0,
  input  B0,
  output S3,
  output S2,
  output S1,
  output S0,
  output C
);

  wire \一位二进制全加器_2_c0 , \一位二进制全加器_3_c0 , \一位二进制全加器_4_c0 ;

  \一位二进制全加器  \u_一位二进制全加器_1  (.A(A3), .B(B3), .Ci(\一位二进制全加器_2_c0 ), .S(S3), .C0(C));
  \一位二进制全加器  \u_一位二进制全加器_2  (.A(A2), .B(B2), .Ci(\一位二进制全加器_3_c0 ), .S(S2), .C0(\一位二进制全加器_2_c0 ));
  \一位二进制全加器  \u_一位二进制全加器_3  (.A(A1), .B(B1), .Ci(\一位二进制全加器_4_c0 ), .S(S1), .C0(\一位二进制全加器_3_c0 ));
  \一位二进制全加器  \u_一位二进制全加器_4  (.A(A0), .B(B0), .Ci(C0), .S(S0), .C0(\一位二进制全加器_4_c0 ));

  // Notes on the sheet:
  //   串行进位的四位二进制并行加法器
endmodule

module \先行进位并行加法器  (
  input  A0,
  input  A1,
  input  A2,
  input  A3,
  input  B0,
  input  B1,
  input  B2,
  input  B3,
  input  C0,
  output S0,
  output S1,
  output S2,
  output S3,
  output C4
);

  wire and_1_out, and_2_out, and_3_out, and_4_out, and_5_out, and_6_out, and_7_out, and_8_out, and_9_out,
       and_10_out, and_11_out, and_12_out, and_13_out, and_14_out, or_1_out, or_2_out, or_3_out, xor_1_out,
       xor_2_out, xor_3_out, xor_4_out, xor_5_out, xor_6_out, xor_7_out, xor_8_out, xor_9_out, xor_10_out,
       xor_11_out, xor_12_out, xor_13_out, xor_14_out, xor_15_out, xor_16_out, xor_17_out, xor_18_out,
       xor_19_out, xor_20_out;

  xor xor_1 (xor_1_out, A0, B0);
  xor xor_2 (xor_2_out, A1, B1);
  xor xor_3 (xor_3_out, A0, B0);
  xor xor_4 (xor_4_out, A1, B1);
  xor xor_5 (xor_5_out, A2, B2);
  xor xor_6 (xor_6_out, A1, B1);
  xor xor_7 (xor_7_out, A0, B0);
  xor xor_8 (xor_8_out, A2, B2);
  xor xor_9 (xor_9_out, A1, B1);
  xor xor_10 (xor_10_out, A2, B2);
  xor xor_11 (xor_11_out, A3, B3);
  xor xor_12 (xor_12_out, A2, B2);
  xor xor_13 (xor_13_out, A1, B1);
  xor xor_14 (xor_14_out, A0, B0);
  xor xor_15 (xor_15_out, A3, B3);
  xor xor_16 (xor_16_out, A2, B2);
  xor xor_17 (xor_17_out, A1, B1);
  xor xor_18 (xor_18_out, A3, B3);
  xor xor_19 (xor_19_out, A2, B2);
  xor xor_20 (xor_20_out, A3, B3);
  xor xor_21 (S0, A0, B0, C0);
  and and_1 (and_1_out, xor_1_out, C0);
  and and_2 (and_2_out, A0, B0);
  and and_3 (and_3_out, xor_2_out, xor_3_out, C0);
  and and_4 (and_4_out, A0, B0, xor_4_out);
  and and_5 (and_5_out, A1, B1);
  and and_6 (and_6_out, xor_5_out, xor_6_out, xor_7_out, C0);
  and and_7 (and_7_out, xor_8_out, xor_9_out, A0, B0);
  and and_8 (and_8_out, A1, B1, xor_10_out);
  and and_9 (and_9_out, A2, B2);
  and and_10 (and_10_out, xor_11_out, xor_12_out, xor_13_out, xor_14_out, C0);
  and and_11 (and_11_out, xor_15_out, xor_16_out, xor_17_out, A0, B0);
  and and_12 (and_12_out, xor_18_out, xor_19_out, A1, B1);
  and and_13 (and_13_out, A2, B2, xor_20_out);
  and and_14 (and_14_out, A3, B3);
  or or_1 (or_1_out, and_1_out, and_2_out);
  or or_2 (or_2_out, and_3_out, and_4_out, and_5_out);
  or or_3 (or_3_out, and_6_out, and_7_out, and_8_out, and_9_out);
  or or_4 (C4, and_10_out, and_11_out, and_12_out, and_13_out, and_14_out);
  xor xor_22 (S1, A1, B1, or_1_out);
  xor xor_23 (S2, A2, B2, or_2_out);
  xor xor_24 (S3, A3, B3, or_3_out);
endmodule

module \先行进位并行加法器测试电路  (
  input  in_1,
  input  in_2,
  input  in_3,
  input  in_4,
  input  in_5,
  input  in_6,
  input  in_7,
  input  in_8,
  input  in_9,
  output out_10,
  output out_11,
  output out_12,
  output out_13,
  output out_14
);

  \先行进位并行加法器  \u_先行进位并行加法器_1  (
    .A0(in_8), .A1(in_6), .A2(in_4), .A3(in_2), .B0(in_3), .B1(in_5), .B2(in_7), .B3(in_9), .C0(in_1),
    .S0(out_13), .S1(out_12), .S2(out_11), .S3(out_10), .C4(out_14));
endmodule

module \四位二进制可逆计数器  (
  input  CPd,
  input  LD,
  input  A,
  input  B,
  input  C,
  input  CLR,
  input  CPu,
  input  D,
  output QA,
  output QB,
  output QC,
  output QD
);

  wire and_1_out, and_2_out, and_3_out, and_4_out, and_5_out, and_6_out, and_7_out, and_8_out, and_9_out,
       and_10_out, and_11_out, and_12_out, and_13_out, and_14_out, d_ff_1_qn, d_ff_2_qn, d_ff_3_qn,
       d_ff_4_qn, or_1_out, or_2_out, or_3_out, or_4_out, or_5_out, or_6_out, or_7_out, or_8_out;

  or or_1 (or_1_out, CPd, CPu);
  and and_1 (and_1_out, d_ff_1_qn, CPd);
  or or_2 (or_2_out, and_1_out, and_2_out);
  and and_2 (and_2_out, CPu, ~d_ff_1_qn);  // AND_Gate
  and and_3 (and_3_out, d_ff_2_qn, d_ff_1_qn, CPd);
  and and_4 (and_4_out, ~d_ff_2_qn, ~d_ff_1_qn, CPu);  // AND_Gate
  and and_5 (and_5_out, d_ff_3_qn, d_ff_2_qn, d_ff_1_qn, CPd);
  and and_6 (and_6_out, ~d_ff_3_qn, ~d_ff_2_qn, ~d_ff_1_qn, CPu);  // AND_Gate
  or or_3 (or_3_out, and_3_out, and_4_out);
  or or_4 (or_4_out, and_5_out, and_6_out);
  D_Flip_Flop #(.trigger("falling")) d_ff_1 (
    .clk(or_1_out), .D(d_ff_1_qn), .Q(QA), .Qn(d_ff_1_qn), .preset(and_13_out), .reset(or_7_out));  // open: en
  D_Flip_Flop #(.trigger("falling")) d_ff_2 (
    .clk(or_2_out), .D(d_ff_2_qn), .Q(QB), .Qn(d_ff_2_qn), .preset(and_7_out), .reset(or_5_out));  // open: en
  or or_5 (or_5_out, and_8_out, CLR);
  D_Flip_Flop #(.trigger("falling")) d_ff_3 (
    .clk(or_3_out), .D(d_ff_3_qn), .Q(QC), .Qn(d_ff_3_qn), .preset(and_10_out), .reset(or_6_out));  // open: en
  or or_6 (or_6_out, and_9_out, CLR);
  D_Flip_Flop #(.trigger("falling")) d_ff_4 (
    .clk(or_4_out), .D(d_ff_4_qn), .Q(QD), .Qn(d_ff_4_qn), .preset(and_14_out), .reset(or_8_out));  // open: en
  or or_7 (or_7_out, and_12_out, CLR);
  and and_7 (and_7_out, ~LD, ~CLR, B);  // AND_Gate
  and and_8 (and_8_out, ~B, ~LD);  // AND_Gate
  and and_9 (and_9_out, ~LD, ~C);  // AND_Gate
  and and_10 (and_10_out, ~CLR, ~LD, C);  // AND_Gate
  and and_11 (and_11_out, ~LD, ~D);  // AND_Gate
  or or_8 (or_8_out, CLR, and_11_out);
  and and_12 (and_12_out, ~LD, ~A);  // AND_Gate
  and and_13 (and_13_out, A, ~LD, ~CLR);  // AND_Gate
  and and_14 (and_14_out, ~CLR, ~LD, D);  // AND_Gate
endmodule

module \四位二进制可逆计数器测试电路  (
  input  in_1,
  input  in_2,
  input  in_3,
  input  in_4,
  input  in_5,
  input  in_6,
  input  in_7,
  input  in_8,
  output out_9,
  output out_10,
  output out_11,
  output out_12
);

  \四位二进制可逆计数器  \u_四位二进制可逆计数器_1  (
    .CPd(in_3), .CPu(in_1), .QA(out_12), .LD(in_8), .A(in_7), .QB(out_11), .B(in_6), .QC(out_10), .C(in_5),
    .CLR(in_2), .QD(out_9), .D(in_4));
endmodule

module \二进制转8421码电路  (
  input  in_1,
  input  in_2,
  input  in_3,
  input  in_4,
  output out_5,
  output out_6,
  output out_7,
  output out_8,
  output out_9,
  output out_10,
  output out_11,
  output out_12
);

  wire and_1_out, or_1_out;

  \先行进位并行加法器  \u_先行进位并行加法器_1  (
    .A0(in_4), .A1(in_3), .A2(in_2), .A3(in_1), .B0(1'b0), .B1(and_1_out), .B2(and_1_out), .B3(1'b0),
    .C0(1'b0), .S0(out_12), .S1(out_11), .S2(out_10), .S3(out_9), .C4(out_8));
  or or_1 (or_1_out, in_2, in_3);
  and and_1 (and_1_out, or_1_out, in_1);

  assign out_5 = 1'b0;
  assign out_6 = 1'b0;
  assign out_7 = 1'b0;
endmodule

module \二进制转8421码测试电路  (
  input  in_1,
  input  in_2,
  input  in_3,
  input  in_4,
  output out_5,
  output out_6,
  output out_7,
  output out_8,
  output out_9,
  output out_10,
  output out_11,
  output out_12
);

  \二进制转8421码电路  \u_二进制转8421码电路_1  (
    .in_1(in_1), .in_2(in_2), .in_3(in_3), .in_4(in_4), .out_5(out_5), .out_6(out_6), .out_7(out_7),
    .out_8(out_8), .out_9(out_9), .out_10(out_10), .out_11(out_11), .out_12(out_12));
endmodule

module \显示电路  (
  input  A3,
  input  A2,
  input  A1,
  input  A0,
  output a,
  output b,
  output c,
  output d,
  output e,
  output f,
  output g
);

  wire and_1_out, and_2_out, and_3_out, and_4_out, and_5_out, and_6_out, and_7_out, and_8_out, and_9_out,
       and_10_out, and_11_out, and_12_out, and_13_out, and_14_out, and_15_out, and_16_out, and_17_out,
       and_18_out, and_19_out, and_20_out, and_21_out, and_22_out, and_23_out, and_24_out, and_25_out,
       and_26_out, not_1_out, not_2_out, not_3_out, not_4_out, not_5_out, not_6_out, not_7_out, not_8_out,
       not_9_out, not_10_out, not_11_out, not_12_out, not_13_out, not_14_out, not_15_out, not_16_out,
       not_17_out, not_18_out, not_19_out, not_20_out, not_21_out, not_22_out, not_23_out, not_24_out,
       not_25_out, not_26_out, not_27_out, not_28_out, not_29_out, not_30_out, not_31_out, not_32_out,
       not_33_out, not_34_out, not_35_out, not_36_out, not_37_out;

  not not_1 (not_1_out, A3);
  not not_2 (not_2_out, A2);
  and and_1 (and_1_out, not_1_out, not_2_out, not_3_out);
  not not_3 (not_3_out, A0);
  not not_4 (not_4_out, A3);
  not not_5 (not_5_out, A2);
  and and_2 (and_2_out, not_4_out, not_5_out, A1);
  not not_6 (not_6_out, A3);
  and and_3 (and_3_out, not_6_out, A2, A0);
  and and_4 (and_4_out, A3, not_7_out, not_8_out);
  not not_7 (not_7_out, A2);
  not not_8 (not_8_out, A1);
  not not_9 (not_9_out, A1);
  and and_5 (and_5_out, A3, not_9_out, A0);
  not not_10 (not_10_out, A3);
  and and_6 (and_6_out, not_10_out, not_11_out);
  not not_11 (not_11_out, A2);
  not not_12 (not_12_out, A2);
  and and_7 (and_7_out, not_12_out, not_13_out);
  not not_13 (not_13_out, A1);
  not not_14 (not_14_out, A1);
  and and_8 (and_8_out, not_14_out, not_15_out);
  not not_15 (not_15_out, A0);
  not not_16 (not_16_out, A3);
  and and_9 (and_9_out, not_16_out, A1, A0);
  not not_17 (not_17_out, A2);
  and and_10 (and_10_out, not_17_out, not_18_out);
  not not_18 (not_18_out, A1);
  not not_19 (not_19_out, A2);
  and and_11 (and_11_out, not_19_out, A0);
  not not_20 (not_20_out, A3);
  and and_12 (and_12_out, not_20_out, A2);
  not not_21 (not_21_out, A2);
  and and_13 (and_13_out, not_21_out, not_22_out);
  not not_22 (not_22_out, A0);
  not not_23 (not_23_out, A2);
  and and_14 (and_14_out, not_23_out, A1);
  and and_15 (and_15_out, A1, not_24_out);
  not not_24 (not_24_out, A0);
  and and_16 (and_16_out, A2, not_25_out, A0);
  not not_25 (not_25_out, A1);
  not not_26 (not_26_out, A2);
  and and_17 (and_17_out, not_26_out, not_27_out);
  not not_27 (not_27_out, A0);
  and and_18 (and_18_out, A1, not_28_out);
  not not_28 (not_28_out, A0);
  not not_29 (not_29_out, A1);
  and and_19 (and_19_out, not_29_out, not_30_out);
  not not_30 (not_30_out, A0);
  and and_20 (and_20_out, A2, not_31_out);
  not not_31 (not_31_out, A1);
  and and_21 (and_21_out, A2, not_32_out);
  not not_32 (not_32_out, A0);
  and and_22 (and_22_out, A3, not_33_out);
  not not_33 (not_33_out, A1);
  not not_34 (not_34_out, A2);
  and and_23 (and_23_out, not_34_out, A1);
  and and_24 (and_24_out, A2, not_35_out);
  not not_35 (not_35_out, A1);
  and and_25 (and_25_out, A2, not_36_out);
  not not_36 (not_36_out, A0);
  and and_26 (and_26_out, A3, not_37_out);
  not not_37 (not_37_out, A2);
  or or_1 (c, and_10_out, and_11_out, and_12_out);
  or or_2 (e, and_17_out, and_18_out);
  or or_3 (a, and_1_out, and_2_out, and_3_out, and_4_out, and_5_out);
  or or_4 (b, and_6_out, and_7_out, and_8_out, and_9_out);
  or or_5 (d, and_13_out, and_14_out, and_15_out, and_16_out);
  or or_6 (f, and_19_out, and_20_out, and_21_out, and_22_out);
  or or_7 (g, and_23_out, and_24_out, and_25_out, and_26_out);
endmodule

module \显示电路测试电路  (
  input  in_1,
  input  in_2,
  input  in_3,
  input  in_4
);

  wire \二进制转8421码电路_1_out_5 , \二进制转8421码电路_1_out_6 , \二进制转8421码电路_1_out_7 , \二进制转8421码电路_1_out_8 ,
       \二进制转8421码电路_1_out_9 , \二进制转8421码电路_1_out_10 , \二进制转8421码电路_1_out_11 , \二进制转8421码电路_1_out_12 ,
       \显示电路_1_a , \显示电路_1_b , \显示电路_1_c , \显示电路_1_d , \显示电路_1_e , \显示电路_1_f , \显示电路_1_g , \显示电路_2_a ,
       \显示电路_2_b , \显示电路_2_c , \显示电路_2_d , \显示电路_2_e , \显示电路_2_f , \显示电路_2_g ;

  _7_Segment_Display u_7_segment_display_1 (
    .g(\显示电路_1_g ), .f(\显示电路_1_f ), .a(\显示电路_1_a ), .b(\显示电路_1_b ), .e(\显示电路_1_e ), .d(\显示电路_1_d ),
    .c(\显示电路_1_c ), .dp(1'b0));
  \显示电路  \u_显示电路_1  (
    .A3(\二进制转8421码电路_1_out_5 ), .A2(\二进制转8421码电路_1_out_6 ), .A1(\二进制转8421码电路_1_out_7 ),
    .A0(\二进制转8421码电路_1_out_8 ), .a(\显示电路_1_a ), .b(\显示电路_1_b ), .c(\显示电路_1_c ), .d(\显示电路_1_d ),
    .e(\显示电路_1_e ), .f(\显示电路_1_f ), .g(\显示电路_1_g ));
  _7_Segment_Display u_7_segment_display_2 (
    .g(\显示电路_2_g ), .f(\显示电路_2_f ), .a(\显示电路_2_a ), .b(\显示电路_2_b ), .e(\显示电路_2_e ), .d(\显示电路_2_d ),
    .c(\显示电路_2_c ), .dp(1'b0));
  \二进制转8421码电路  \u_二进制转8421码电路_1  (
    .in_1(in_1), .in_2(in_2), .in_3(in_3), .in_4(in_4), .out_5(\二进制转8421码电路_1_out_5 ),
    .out_6(\二进制转8421码电路_1_out_6 ), .out_7(\二进制转8421码电路_1_out_7 ), .out_8(\二进制转8421码电路_1_out_8 ),
    .out_9(\二进制转8421码电路_1_out_9 ), .out_10(\二进制转8421码电路_1_out_10 ), .out_11(\二进制转8421码电路_1_out_11 ),
    .out_12(\二进制转8421码电路_1_out_12 ));
  \显示电路  \u_显示电路_2  (
    .A3(\二进制转8421码电路_1_out_9 ), .A2(\二进制转8421码电路_1_out_10 ), .A1(\二进制转8421码电路_1_out_11 ),
    .A0(\二进制转8421码电路_1_out_12 ), .a(\显示电路_2_a ), .b(\显示电路_2_b ), .c(\显示电路_2_c ), .d(\显示电路_2_d ),
    .e(\显示电路_2_e ), .f(\显示电路_2_f ), .g(\显示电路_2_g ));
endmodule

module \报警电路  (
  input  in_1,
  input  in_2,
  input  in_3,
  output out_4,
  output out_5,
  output out_6,
  output out_7,
  output out_8
);

  wire and_2_out, and_3_out, and_4_out, or_1_out;

  and and_1 (out_4, and_2_out, in_1);
  and and_2 (and_2_out, out_8, out_7, out_6, out_5);
  and and_3 (and_3_out, ~and_2_out, in_1);  // AND_Gate
  and and_4 (and_4_out, or_1_out, in_3);
  or or_1 (or_1_out, out_5, out_6, out_7, out_8);
  \四位二进制可逆计数器  \u_四位二进制可逆计数器_1  (
    .CPd(and_4_out), .CPu(and_3_out), .QA(out_8), .LD(1'b1), .A(1'b0), .QB(out_7), .B(1'b0), .QC(out_6),
    .C(1'b0), .CLR(in_2), .QD(out_5), .D(1'b0));
endmodule

module \小型实验室门禁系统  (
  input  in_1,
  input  in_2,
  input  in_3,
  output out_4,
  output out_5,
  output out_6,
  output out_7,
  output out_8,
  output out_9,
  output out_10,
  output out_11,
  output out_12,
  output out_13,
  output out_14,
  output out_15,
  output out_16,
  output out_17,
  output out_18
);

  wire \二进制转8421码电路_1_out_5 , \二进制转8421码电路_1_out_6 , \二进制转8421码电路_1_out_7 , \二进制转8421码电路_1_out_8 ,
       \二进制转8421码电路_1_out_9 , \二进制转8421码电路_1_out_10 , \二进制转8421码电路_1_out_11 , \二进制转8421码电路_1_out_12 ,
       \报警电路_1_out_5 , \报警电路_1_out_6 , \报警电路_1_out_7 , \报警电路_1_out_8 ;

  \显示电路  \u_显示电路_1  (
    .A3(\二进制转8421码电路_1_out_5 ), .A2(\二进制转8421码电路_1_out_6 ), .A1(\二进制转8421码电路_1_out_7 ),
    .A0(\二进制转8421码电路_1_out_8 ), .a(out_4), .b(out_5), .c(out_6), .d(out_7), .e(out_8), .f(out_9), .g(out_10));
  \报警电路  \u_报警电路_1  (
    .in_1(in_1), .in_2(in_2), .in_3(in_3), .out_4(out_18), .out_5(\报警电路_1_out_5 ), .out_6(\报警电路_1_out_6 ),
    .out_7(\报警电路_1_out_7 ), .out_8(\报警电路_1_out_8 ));
  \二进制转8421码电路  \u_二进制转8421码电路_1  (
    .in_1(\报警电路_1_out_5 ), .in_2(\报警电路_1_out_6 ), .in_3(\报警电路_1_out_7 ), .in_4(\报警电路_1_out_8 ),
    .out_5(\二进制转8421码电路_1_out_5 ), .out_6(\二进制转8421码电路_1_out_6 ), .out_7(\二进制转8421码电路_1_out_7 ),
    .out_8(\二进制转8421码电路_1_out_8 ), .out_9(\二进制转8421码电路_1_out_9 ), .out_10(\二进制转8421码电路_1_out_10 ),
    .out_11(\二进制转8421码电路_1_out_11 ), .out_12(\二进制转8421码电路_1_out_12 ));
  \显示电路  \u_显示电路_2  (
    .A3(\二进制转8421码电路_1_out_9 ), .A2(\二进制转8421码电路_1_out_10 ), .A1(\二进制转8421码电路_1_out_11 ),
    .A0(\二进制转8421码电路_1_out_12 ), .a(out_11), .b(out_12), .c(out_13), .d(out_14), .e(out_15), .f(out_16),
    .g(out_17));
endmodule

module \小型门禁系统测试电路  (
  input  in_1,
  input  in_2,
  input  in_3
);

  wire \小型实验室门禁系统_1_out_4 , \小型实验室门禁系统_1_out_5 , \小型实验室门禁系统_1_out_6 , \小型实验室门禁系统_1_out_7 ,
       \小型实验室门禁系统_1_out_8 , \小型实验室门禁系统_1_out_9 , \小型实验室门禁系统_1_out_10 , \小型实验室门禁系统_1_out_11 ,
       \小型实验室门禁系统_1_out_12 , \小型实验室门禁系统_1_out_13 , \小型实验室门禁系统_1_out_14 , \小型实验室门禁系统_1_out_15 ,
       \小型实验室门禁系统_1_out_16 , \小型实验室门禁系统_1_out_17 , \小型实验室门禁系统_1_out_18 ;

  _7_Segment_Display u_7_segment_display_1 (
    .g(\小型实验室门禁系统_1_out_10 ), .f(\小型实验室门禁系统_1_out_9 ), .a(\小型实验室门禁系统_1_out_4 ), .b(\小型实验室门禁系统_1_out_5 ),
    .e(\小型实验室门禁系统_1_out_8 ), .d(\小型实验室门禁系统_1_out_7 ), .c(\小型实验室门禁系统_1_out_6 ), .dp(1'b0));
  \小型实验室门禁系统  \u_小型实验室门禁系统_1  (
    .in_1(in_1), .in_2(in_2), .in_3(in_3), .out_4(\小型实验室门禁系统_1_out_4 ), .out_5(\小型实验室门禁系统_1_out_5 ),
    .out_6(\小型实验室门禁系统_1_out_6 ), .out_7(\小型实验室门禁系统_1_out_7 ), .out_8(\小型实验室门禁系统_1_out_8 ),
    .out_9(\小型实验室门禁系统_1_out_9 ), .out_10(\小型实验室门禁系统_1_out_10 ), .out_11(\小型实验室门禁系统_1_out_11 ),
    .out_12(\小型实验室门禁系统_1_out_12 ), .out_13(\小型实验室门禁系统_1_out_13 ), .out_14(\小型实验室门禁系统_1_out_14 ),
    .out_15(\小型实验室门禁系统_1_out_15 ), .out_16(\小型实验室门禁系统_1_out_16 ), .out_17(\小型实验室门禁系统_1_out_17 ),
    .out_18(\小型实验室门禁系统_1_out_18 ));
  _7_Segment_Display u_7_segment_display_2 (
    .g(\小型实验室门禁系统_1_out_17 ), .f(\小型实验室门禁系统_1_out_16 ), .a(\小型实验室门禁系统_1_out_11 ), .b(\小型实验室门禁系统_1_out_12 ),
    .e(\小型实验室门禁系统_1_out_15 ), .d(\小型实验室门禁系统_1_out_14 ), .c(\小型实验室门禁系统_1_out_13 ), .dp(1'b0));
  LED led_1 (.in(\小型实验室门禁系统_1_out_18 ));
endmodule
