// Logisim project 实验3.circ as structural Verilog: 7 circuits, main circuit 四位乘法器
module \四位乘法器  (
  input  [3:0] in_1,
  input  [3:0] b_3_0,
  output [7:0] out_3
);

  wire [7:0] adder_1_out, adder_2_out, adder_3_out, adder_4_out, bit_extender_1_out, multiplexer_1_out,
       multiplexer_2_out, multiplexer_3_out, shifter_1_out, shifter_2_out, shifter_3_out;

  assign bit_extender_1_out = {{4{1'b0}}, b_3_0};  // Bit_Extender bit_extender_1
  Adder #(.width(8)) adder_1 (.a({8{1'b0}}), .b(bit_extender_1_out), .out(adder_1_out));  // open: cin, cout
  Shifter #(.width(8), .shift("ll")) shifter_1 (.in(bit_extender_1_out), .\dist (3'b001), .out(shifter_1_out));
  Multiplexer #(.select(1), .width(8), .disabled("Z"), .enable("false")) multiplexer_1 (
    .in0({8{1'b0}}), .in1(adder_1_out), .out(multiplexer_1_out), .sel(in_1[0]));
  Adder #(.width(8)) adder_2 (.a(multiplexer_1_out), .b(shifter_1_out), .out(adder_2_out));  // open: cin, cout
  Multiplexer #(.select(1), .width(8), .disabled("Z"), .enable("false")) multiplexer_2 (
    .in0(multiplexer_1_out), .in1(adder_2_out), .out(multiplexer_2_out), .sel(in_1[1]));
  Shifter #(.width(8), .shift("ll")) shifter_2 (.in(shifter_1_out), .\dist (3'b001), .out(shifter_2_out));
  Adder #(.width(8)) adder_3 (.a(multiplexer_2_out), .b(shifter_2_out), .out(adder_3_out));  // open: cin, cout
  Shifter #(.width(8), .shift("ll")) shifter_3 (.in(shifter_2_out), .\dist (3'b001), .out(shifter_3_out));
  Multiplexer #(.select(1), .width(8), .disabled("Z"), .enable("false")) multiplexer_3 (
    .in0(multiplexer_2_out), .in1(adder_3_out), .out(multiplexer_3_out), .sel(in_1[2]));
  Adder #(.width(8)) adder_4 (.a(multiplexer_3_out), .b(shifter_3_out), .out(adder_4_out));  // open: cin, cout
  Multiplexer #(.select(1), .width(8), .disabled("Z"), .enable("false")) multiplexer_4 (
    .in0(multiplexer_3_out), .in1(adder_4_out), .out(out_3), .sel(in_1[3]));

  // Notes on the sheet:
  //   a
  //   0
  //   a
  //   1
  //   a
  //   2
  //   a
  //   3
endmodule

module \四位乘法器测试电路  (
  input  [3:0] in_1,
  input  [3:0] in_2,
  input  [3:0] in_3,
  input  [3:0] in_4,
  output [7:0] out_5,
  output [3:0] out_6,
  output [3:0] out_7
);

  Multiplier #(.width(4)) multiplier_1 (.a(in_3), .b(in_4), .out(out_6), .cout(out_7));  // open: cin
  \四位乘法器  \u_四位乘法器_1  (.b_3_0(in_2), .out_3(out_5), .in_1(in_1));

  // Notes on the sheet:
  //   对比内部乘法器电路
  //   四位乘法器测试电路
endmodule

module \_32_4乘法器  (
  input  [3:0] in_1,
  input  [31:0] in_2,
  output [31:0] out_3,
  output [31:0] out_4
);

  wire [31:0] adder_1_out, adder_2_out, adder_3_out, adder_4_out, adder_5_out, adder_6_out, adder_7_out,
       adder_8_out, multiplexer_1_out, multiplexer_2_out, multiplexer_3_out, multiplexer_4_out,
       multiplexer_5_out, multiplexer_6_out, \n64位移位器_自己设计_1_out_4 , \n64位移位器_自己设计_1_out_5 ,
       \n64位移位器_自己设计_2_out_4 , \n64位移位器_自己设计_2_out_5 , \n64位移位器_自己设计_3_out_4 , \n64位移位器_自己设计_3_out_5 ;

  Adder #(.width(32)) adder_1 (.a({32{1'b0}}), .b({32{1'b0}}), .out(adder_1_out));  // open: cin, cout
  Adder #(.width(32)) adder_2 (.a({32{1'b0}}), .b(in_2), .out(adder_2_out));  // open: cin, cout
  Multiplexer #(.select(1), .width(32), .disabled("Z"), .enable("false")) multiplexer_1 (
    .in0({32{1'b0}}), .in1(adder_1_out), .out(multiplexer_1_out), .sel(in_1[0]));
  Multiplexer #(.select(1), .width(32), .disabled("Z"), .enable("false")) multiplexer_2 (
    .in0({32{1'b0}}), .in1(adder_2_out), .out(multiplexer_2_out), .sel(in_1[0]));
  \_64位移位器_自己设计  \u_64位移位器_自己设计_1  (
    .in_1({32{1'b0}}), .in_2(5'b00001), .in_3(in_2), .out_4(\n64位移位器_自己设计_1_out_4 ),
    .out_5(\n64位移位器_自己设计_1_out_5 ));
  Adder #(.width(32)) adder_3 (
    .a(multiplexer_1_out), .b(\n64位移位器_自己设计_1_out_4 ), .out(adder_3_out));  // open: cin, cout
  Adder #(.width(32)) adder_4 (
    .a(multiplexer_2_out), .b(\n64位移位器_自己设计_1_out_5 ), .out(adder_4_out));  // open: cin, cout
  Multiplexer #(.select(1), .width(32), .disabled("Z"), .enable("false")) multiplexer_3 (
    .in0(multiplexer_2_out), .in1(adder_4_out), .out(multiplexer_3_out), .sel(in_1[1]));
  Multiplexer #(.select(1), .width(32), .disabled("Z"), .enable("false")) multiplexer_4 (
    .in0(multiplexer_1_out), .in1(adder_3_out), .out(multiplexer_4_out), .sel(in_1[1]));
  \_64位移位器_自己设计  \u_64位移位器_自己设计_2  (
    .in_1(\n64位移位器_自己设计_1_out_4 ), .in_2(5'b00001), .in_3(\n64位移位器_自己设计_1_out_5 ),
    .out_4(\n64位移位器_自己设计_2_out_4 ), .out_5(\n64位移位器_自己设计_2_out_5 ));
  Adder #(.width(32)) adder_5 (
    .a(multiplexer_4_out), .b(\n64位移位器_自己设计_2_out_4 ), .out(adder_5_out));  // open: cin, cout
  Adder #(.width(32)) adder_6 (
    .a(multiplexer_3_out), .b(\n64位移位器_自己设计_2_out_5 ), .out(adder_6_out));  // open: cin, cout
  \_64位移位器_自己设计  \u_64位移位器_自己设计_3  (
    .in_1(\n64位移位器_自己设计_2_out_4 ), .in_2(5'b00001), .in_3(\n64位移位器_自己设计_2_out_5 ),
    .out_4(\n64位移位器_自己设计_3_out_4 ), .out_5(\n64位移位器_自己设计_3_out_5 ));
  Multiplexer #(.select(1), .width(32), .disabled("Z"), .enable("false")) multiplexer_5 (
    .in0(multiplexer_4_out), .in1(adder_5_out), .out(multiplexer_5_out), .sel(in_1[2]));
  Multiplexer #(.select(1), .width(32), .disabled("Z"), .enable("false")) multiplexer_6 (
    .in0(multiplexer_3_out), .in1(adder_6_out), .out(multiplexer_6_out), .sel(in_1[2]));
  Adder #(.width(32)) adder_7 (
    .a(multiplexer_5_out), .b(\n64位移位器_自己设计_3_out_4 ), .out(adder_7_out));  // open: cin, cout
  Adder #(.width(32)) adder_8 (
    .a(multiplexer_6_out), .b(\n64位移位器_自己设计_3_out_5 ), .out(adder_8_out));  // open: cin, cout
  Multiplexer #(.select(1), .width(32), .disabled("Z"), .enable("false")) multiplexer_7 (
    .in0(multiplexer_5_out), .in1(adder_7_out), .out(out_3), .sel(in_1[3]));
  Multiplexer #(.select(1), .width(32), .disabled("Z"), .enable("false")) multiplexer_8 (
    .in0(multiplexer_6_out), .in1(adder_8_out), .out(out_4), .sel(in_1[3]));

  // Notes on the sheet:
  //   b(32:0)
endmodule

module \_32_4乘法器测试电路  (
  input  [3:0] in_1,
  input  [31:0] in_2,
  input  [31:0] in_3,
  input  [31:0] in_4,
  output [31:0] out_5,
  output [31:0] out_6,
  output [31:0] out_7,
  output [31:0] out_8
);

  Multiplier #(.width(32)) multiplier_1 (.a(in_3), .b(in_4), .out(out_7), .cout(out_8));  // open: cin
  \_32_4乘法器  \u_32_4乘法器_1  (.in_1(in_1), .in_2(in_2), .out_3(out_5), .out_4(out_6));

  // Notes on the sheet:
  //   32×4乘法器测试电路
  //   对比内部乘法器电路
endmodule

module \_32_32乘法器  (
  input  [31:0] in_1,
  input  [31:0] in_2,
  output [31:0] out_3,
  output [31:0] out_4
);

  wire adder_2_cout, adder_3_cout, adder_5_cout, adder_6_cout, adder_8_cout, adder_10_cout, adder_13_cout;
  wire [31:0] adder_1_out, adder_2_out, adder_3_out, adder_4_out, adder_5_out, adder_6_out, adder_7_out,
       adder_8_out, adder_11_out, adder_12_out, adder_13_out, adder_14_out, \n32_4乘法器_1_out_3 ,
       \n32_4乘法器_1_out_4 , \n32_4乘法器_2_out_3 , \n32_4乘法器_2_out_4 , \n32_4乘法器_3_out_3 , \n32_4乘法器_3_out_4 ,
       \n32_4乘法器_4_out_3 , \n32_4乘法器_4_out_4 , \n32_4乘法器_5_out_3 , \n32_4乘法器_5_out_4 , \n32_4乘法器_6_out_3 ,
       \n32_4乘法器_6_out_4 , \n32_4乘法器_7_out_3 , \n32_4乘法器_7_out_4 , \n32_4乘法器_8_out_3 , \n32_4乘法器_8_out_4 ,
       \n64位移位器_自己设计_1_out_4 , \n64位移位器_自己设计_1_out_5 , \n64位移位器_自己设计_2_out_4 , \n64位移位器_自己设计_2_out_5 ,
       \n64位移位器_自己设计_3_out_4 , \n64位移位器_自己设计_3_out_5 , \n64位移位器_自己设计_4_out_4 , \n64位移位器_自己设计_4_out_5 ,
       \n64位移位器_自己设计_5_out_4 , \n64位移位器_自己设计_5_out_5 , \n64位移位器_自己设计_6_out_4 , \n64位移位器_自己设计_6_out_5 ,
       \n64位移位器_自己设计_7_out_4 , \n64位移位器_自己设计_7_out_5 ;

  \_32_4乘法器  \u_32_4乘法器_1  (.in_1(in_1[3:0]), .in_2(in_2), .out_3(\n32_4乘法器_1_out_3 ), .out_4(\n32_4乘法器_1_out_4 ));
  \_32_4乘法器  \u_32_4乘法器_2  (.in_1(in_1[7:4]), .in_2(in_2), .out_3(\n32_4乘法器_2_out_3 ), .out_4(\n32_4乘法器_2_out_4 ));
  \_32_4乘法器  \u_32_4乘法器_3  (.in_1(in_1[11:8]), .in_2(in_2), .out_3(\n32_4乘法器_3_out_3 ), .out_4(\n32_4乘法器_3_out_4 ));
  \_32_4乘法器  \u_32_4乘法器_4  (.in_1(in_1[15:12]), .in_2(in_2), .out_3(\n32_4乘法器_4_out_3 ), .out_4(\n32_4乘法器_4_out_4 ));
  \_32_4乘法器  \u_32_4乘法器_5  (.in_1(in_1[19:16]), .in_2(in_2), .out_3(\n32_4乘法器_5_out_3 ), .out_4(\n32_4乘法器_5_out_4 ));
  \_32_4乘法器  \u_32_4乘法器_6  (.in_1(in_1[23:20]), .in_2(in_2), .out_3(\n32_4乘法器_6_out_3 ), .out_4(\n32_4乘法器_6_out_4 ));
  \_32_4乘法器  \u_32_4乘法器_7  (.in_1(in_1[27:24]), .in_2(in_2), .out_3(\n32_4乘法器_7_out_3 ), .out_4(\n32_4乘法器_7_out_4 ));
  \_32_4乘法器  \u_32_4乘法器_8  (.in_1(in_1[31:28]), .in_2(in_2), .out_3(\n32_4乘法器_8_out_3 ), .out_4(\n32_4乘法器_8_out_4 ));
  \_64位移位器_自己设计  \u_64位移位器_自己设计_1  (
    .in_1(\n32_4乘法器_2_out_3 ), .in_2(5'b00100), .in_3(\n32_4乘法器_2_out_4 ), .out_4(\n64位移位器_自己设计_1_out_4 ),
    .out_5(\n64位移位器_自己设计_1_out_5 ));
  \_64位移位器_自己设计  \u_64位移位器_自己设计_2  (
    .in_1(\n32_4乘法器_3_out_3 ), .in_2(5'b01000), .in_3(\n32_4乘法器_3_out_4 ), .out_4(\n64位移位器_自己设计_2_out_4 ),
    .out_5(\n64位移位器_自己设计_2_out_5 ));
  \_64位移位器_自己设计  \u_64位移位器_自己设计_3  (
    .in_1(\n32_4乘法器_4_out_3 ), .in_2(5'b01100), .in_3(\n32_4乘法器_4_out_4 ), .out_4(\n64位移位器_自己设计_3_out_4 ),
    .out_5(\n64位移位器_自己设计_3_out_5 ));
  \_64位移位器_自己设计  \u_64位移位器_自己设计_4  (
    .in_1(\n32_4乘法器_5_out_3 ), .in_2(5'b10000), .in_3(\n32_4乘法器_5_out_4 ), .out_4(\n64位移位器_自己设计_4_out_4 ),
    .out_5(\n64位移位器_自己设计_4_out_5 ));
  \_64位移位器_自己设计  \u_64位移位器_自己设计_5  (
    .in_1(\n32_4乘法器_6_out_3 ), .in_2(5'b10100), .in_3(\n32_4乘法器_6_out_4 ), .out_4(\n64位移位器_自己设计_5_out_4 ),
    .out_5(\n64位移位器_自己设计_5_out_5 ));
  \_64位移位器_自己设计  \u_64位移位器_自己设计_6  (
    .in_1(\n32_4乘法器_7_out_3 ), .in_2(5'b11000), .in_3(\n32_4乘法器_7_out_4 ), .out_4(\n64位移位器_自己设计_6_out_4 ),
    .out_5(\n64位移位器_自己设计_6_out_5 ));
  \_64位移位器_自己设计  \u_64位移位器_自己设计_7  (
    .in_1(\n32_4乘法器_8_out_3 ), .in_2(5'b11100), .in_3(\n32_4乘法器_8_out_4 ), .out_4(\n64位移位器_自己设计_7_out_4 ),
    .out_5(\n64位移位器_自己设计_7_out_5 ));
  Adder #(.width(32)) adder_1 (
    .a(\n32_4乘法器_1_out_3 ), .b(\n64位移位器_自己设计_1_out_4 ), .out(adder_1_out), .cin(adder_2_cout));  // open: cout
  Adder #(.width(32)) adder_2 (
    .a(\n32_4乘法器_1_out_4 ), .b(\n64位移位器_自己设计_1_out_5 ), .out(adder_2_out), .cin(1'b0), .cout(adder_2_cout));
  Adder #(.width(32)) adder_3 (
    .a(\n64位移位器_自己设计_2_out_5 ), .b(adder_2_out), .out(adder_3_out), .cin(1'b0), .cout(adder_3_cout));
  Adder #(.width(32)) adder_4 (
    .a(adder_11_out), .b(\n64位移位器_自己设计_3_out_4 ), .out(adder_4_out), .cin(adder_5_cout));  // open: cout
  Adder #(.width(32)) adder_5 (
    .a(adder_3_out), .b(\n64位移位器_自己设计_3_out_5 ), .out(adder_5_out), .cin(1'b0), .cout(adder_5_cout));
  Adder #(.width(32)) adder_6 (
    .a(adder_13_out), .b(\n64位移位器_自己设计_5_out_5 ), .out(adder_6_out), .cin(1'b0), .cout(adder_6_cout));
  Adder #(.width(32)) adder_7 (
    .a(adder_14_out), .b(\n64位移位器_自己设计_6_out_4 ), .out(adder_7_out), .cin(adder_8_cout));  // open: cout
  Adder #(.width(32)) adder_8 (
    .a(adder_6_out), .b(\n64位移位器_自己设计_6_out_5 ), .out(adder_8_out), .cin(1'b0), .cout(adder_8_cout));
  Adder #(.width(32)) adder_9 (
    .a(adder_7_out), .b(\n64位移位器_自己设计_7_out_4 ), .out(out_3), .cin(adder_10_cout));  // open: cout
  Adder #(.width(32)) adder_10 (
    .a(adder_8_out), .b(\n64位移位器_自己设计_7_out_5 ), .out(out_4), .cin(1'b0), .cout(adder_10_cout));
  Adder #(.width(32)) adder_11 (
    .a(adder_1_out), .b(\n64位移位器_自己设计_2_out_4 ), .out(adder_11_out), .cin(adder_3_cout));  // open: cout
  Adder #(.width(32)) adder_12 (
    .a(adder_4_out), .b(\n64位移位器_自己设计_4_out_4 ), .out(adder_12_out), .cin(adder_13_cout));  // open: cout
  Adder #(.width(32)) adder_13 (
    .a(adder_5_out), .b(\n64位移位器_自己设计_4_out_5 ), .out(adder_13_out), .cin(1'b0), .cout(adder_13_cout));
  Adder #(.width(32)) adder_14 (
    .a(adder_12_out), .b(\n64位移位器_自己设计_5_out_4 ), .out(adder_14_out), .cin(adder_6_cout));  // open: cout
endmodule

module \_32_32乘法器测试电路  (
  input  [31:0] in_1,
  input  [31:0] in_2,
  input  [31:0] in_3,
  input  [31:0] in_4,
  output [31:0] out_5,
  output [31:0] out_6,
  output [31:0] out_7,
  output [31:0] out_8
);

  \_32_32乘法器  \u_32_32乘法器_1  (.in_1(in_1), .in_2(in_2), .out_3(out_5), .out_4(out_6));
  Multiplier #(.width(32)) multiplier_1 (.a(in_3), .b(in_4), .out(out_7), .cout(out_8));  // open: cin

  // Notes on the sheet:
  //   32×32乘法器测试电路
  //   对比内部乘法器电路
endmodule

module \_64位移位器_自己设计  (
  input  [31:0] in_1,
  input  [4:0] in_2,
  input  [31:0] in_3,
  output [31:0] out_4,
  output [31:0] out_5
);

  wire [4:0] adder_1_out, subtractor_1_out;
  wire [31:0] shifter_1_out, shifter_2_out;

  Subtractor #(.width(5)) subtractor_1 (.a({5{1'b1}}), .b(in_2), .out(subtractor_1_out));  // open: bin, bout
  Adder #(.width(5)) adder_1 (.a(subtractor_1_out), .b(5'b00001), .out(adder_1_out));  // open: cin, cout
  Shifter #(.width(32), .shift("ll")) shifter_1 (.in(in_1), .\dist (in_2), .out(shifter_1_out));
  Shifter #(.width(32), .shift("lr")) shifter_2 (.in(in_3), .\dist (adder_1_out), .out(shifter_2_out));
  Shifter #(.width(32), .shift("ll")) shifter_3 (.in(in_3), .\dist (in_2), .out(out_5));
  Adder #(.width(32)) adder_2 (.a(shifter_1_out), .b(shifter_2_out), .out(out_4));  // open: cin, cout

  // Notes on the sheet:
  //   高32位
  //   低32位
  //   移位后的低32位
  //   移位后的高32位
endmodule
