// Logisim project 实验4-CS1805-U201814629-裴涵.circ as structural Verilog: 7 circuits, main circuit 四位除法器基本单元
module \四位除法器  (
  input  [3:0] in_1,
  input  [3:0] in_2,
  output [3:0] out_3,
  output [3:0] out_4
);

  wire [7:0] bit_extender_1_out, \四位除法器基本单元_1_out_3 , \四位除法器基本单元_2_out_3 , \四位除法器基本单元_3_out_3 ;

  assign bit_extender_1_out = {{4{1'b0}}, in_1};  // Bit_Extender bit_extender_1
  \四位除法器基本单元  \u_四位除法器基本单元_1  (.in_1(bit_extender_1_out), .in_2(in_2), .out_3(\四位除法器基本单元_1_out_3 ));
  \四位除法器基本单元  \u_四位除法器基本单元_2  (.in_1(\四位除法器基本单元_1_out_3 ), .in_2(in_2), .out_3(\四位除法器基本单元_2_out_3 ));
  \四位除法器基本单元  \u_四位除法器基本单元_3  (.in_1(\四位除法器基本单元_2_out_3 ), .in_2(in_2), .out_3(\四位除法器基本单元_3_out_3 ));
  \四位除法器基本单元  \u_四位除法器基本单元_4  (.in_1(\四位除法器基本单元_3_out_3 ), .in_2(in_2), .out_3({out_4, out_3}));
endmodule

module \四位除法器测试电路  (
  input  [3:0] in_1,
  input  [3:0] in_2,
  output [3:0] out_3,
  output [3:0] out_4,
  output [3:0] out_5,
  output [3:0] out_6
);

  Divider #(.width(4)) divider_1 (.a(in_1), .b(in_2), .out(out_5), .rem(out_6));  // open: upper
  \四位除法器  \u_四位除法器_1  (.in_1(in_1), .in_2(in_2), .out_3(out_3), .out_4(out_4));
endmodule

module \_32位除法器  (
  input  [31:0] in_1,
  input  [31:0] in_2,
  output [31:0] out_3,
  output [31:0] out_4
);

  wire [31:0] \n32位除法器基本单元_1_out_4 , \n32位除法器基本单元_1_out_5 , \n32位除法器基本单元_2_out_4 , \n32位除法器基本单元_2_out_5 ,
       \n32位除法器基本单元_3_out_4 , \n32位除法器基本单元_3_out_5 , \n32位除法器基本单元_4_out_4 , \n32位除法器基本单元_4_out_5 ,
       \n32位除法器基本单元_5_out_4 , \n32位除法器基本单元_5_out_5 , \n32位除法器基本单元_6_out_4 , \n32位除法器基本单元_6_out_5 ,
       \n32位除法器基本单元_7_out_4 , \n32位除法器基本单元_7_out_5 , \n32位除法器基本单元_8_out_4 , \n32位除法器基本单元_8_out_5 ,
       \n32位除法器基本单元_9_out_4 , \n32位除法器基本单元_9_out_5 , \n32位除法器基本单元_10_out_4 , \n32位除法器基本单元_10_out_5 ,
       \n32位除法器基本单元_11_out_4 , \n32位除法器基本单元_11_out_5 , \n32位除法器基本单元_12_out_4 , \n32位除法器基本单元_12_out_5 ,
       \n32位除法器基本单元_13_out_4 , \n32位除法器基本单元_13_out_5 , \n32位除法器基本单元_14_out_4 , \n32位除法器基本单元_14_out_5 ,
       \n32位除法器基本单元_15_out_4 , \n32位除法器基本单元_15_out_5 , \n32位除法器基本单元_16_out_4 , \n32位除法器基本单元_16_out_5 ,
       \n32位除法器基本单元_17_out_4 , \n32位除法器基本单元_17_out_5 , \n32位除法器基本单元_18_out_4 , \n32位除法器基本单元_18_out_5 ,
       \n32位除法器基本单元_19_out_4 , \n32位除法器基本单元_19_out_5 , \n32位除法器基本单元_20_out_4 , \n32位除法器基本单元_20_out_5 ,
       \n32位除法器基本单元_21_out_4 , \n32位除法器基本单元_21_out_5 , \n32位除法器基本单元_22_out_4 , \n32位除法器基本单元_22_out_5 ,
       \n32位除法器基本单元_23_out_4 , \n32位除法器基本单元_23_out_5 , \n32位除法器基本单元_24_out_4 , \n32位除法器基本单元_24_out_5 ,
       \n32位除法器基本单元_25_out_4 , \n32位除法器基本单元_25_out_5 , \n32位除法器基本单元_26_out_4 , \n32位除法器基本单元_26_out_5 ,
       \n32位除法器基本单元_27_out_4 , \n32位除法器基本单元_27_out_5 , \n32位除法器基本单元_28_out_4 , \n32位除法器基本单元_28_out_5 ,
       \n32位除法器基本单元_29_out_4 , \n32位除法器基本单元_29_out_5 , \n32位除法器基本单元_31_out_4 , \n32位除法器基本单元_31_out_5 ,
       \n32位除法器基本单元_32_out_4 , \n32位除法器基本单元_32_out_5 ;

  \_32位除法器基本单元  \u_32位除法器基本单元_1  (
    .in_2(in_1), .in_3(in_2), .out_4(\n32位除法器基本单元_1_out_4 ), .out_5(\n32位除法器基本单元_1_out_5 ), .in_1({32{1'b0}}));
  \_32位除法器基本单元  \u_32位除法器基本单元_2  (
    .in_2(\n32位除法器基本单元_32_out_5 ), .in_3(in_2), .out_4(\n32位除法器基本单元_2_out_4 ), .out_5(\n32位除法器基本单元_2_out_5 ),
    .in_1(\n32位除法器基本单元_32_out_4 ));
  \_32位除法器基本单元  \u_32位除法器基本单元_3  (
    .in_2(\n32位除法器基本单元_29_out_5 ), .in_3(in_2), .out_4(\n32位除法器基本单元_3_out_4 ), .out_5(\n32位除法器基本单元_3_out_5 ),
    .in_1(\n32位除法器基本单元_29_out_4 ));
  \_32位除法器基本单元  \u_32位除法器基本单元_4  (
    .in_2(\n32位除法器基本单元_1_out_5 ), .in_3(in_2), .out_4(\n32位除法器基本单元_4_out_4 ), .out_5(\n32位除法器基本单元_4_out_5 ),
    .in_1(\n32位除法器基本单元_1_out_4 ));
  \_32位除法器基本单元  \u_32位除法器基本单元_5  (
    .in_2(\n32位除法器基本单元_2_out_5 ), .in_3(in_2), .out_4(\n32位除法器基本单元_5_out_4 ), .out_5(\n32位除法器基本单元_5_out_5 ),
    .in_1(\n32位除法器基本单元_2_out_4 ));
  \_32位除法器基本单元  \u_32位除法器基本单元_6  (
    .in_2(\n32位除法器基本单元_3_out_5 ), .in_3(in_2), .out_4(\n32位除法器基本单元_6_out_4 ), .out_5(\n32位除法器基本单元_6_out_5 ),
    .in_1(\n32位除法器基本单元_3_out_4 ));
  \_32位除法器基本单元  \u_32位除法器基本单元_7  (
    .in_2(\n32位除法器基本单元_4_out_5 ), .in_3(in_2), .out_4(\n32位除法器基本单元_7_out_4 ), .out_5(\n32位除法器基本单元_7_out_5 ),
    .in_1(\n32位除法器基本单元_4_out_4 ));
  \_32位除法器基本单元  \u_32位除法器基本单元_8  (
    .in_2(\n32位除法器基本单元_5_out_5 ), .in_3(in_2), .out_4(\n32位除法器基本单元_8_out_4 ), .out_5(\n32位除法器基本单元_8_out_5 ),
    .in_1(\n32位除法器基本单元_5_out_4 ));
  \_32位除法器基本单元  \u_32位除法器基本单元_9  (
    .in_2(\n32位除法器基本单元_6_out_5 ), .in_3(in_2), .out_4(\n32位除法器基本单元_9_out_4 ), .out_5(\n32位除法器基本单元_9_out_5 ),
    .in_1(\n32位除法器基本单元_6_out_4 ));
  \_32位除法器基本单元  \u_32位除法器基本单元_10  (
    .in_2(\n32位除法器基本单元_7_out_5 ), .in_3(in_2), .out_4(\n32位除法器基本单元_10_out_4 ),
    .out_5(\n32位除法器基本单元_10_out_5 ), .in_1(\n32位除法器基本单元_7_out_4 ));
  \_32位除法器基本单元  \u_32位除法器基本单元_11  (
    .in_2(\n32位除法器基本单元_8_out_5 ), .in_3(in_2), .out_4(\n32位除法器基本单元_11_out_4 ),
    .out_5(\n32位除法器基本单元_11_out_5 ), .in_1(\n32位除法器基本单元_8_out_4 ));
  \_32位除法器基本单元  \u_32位除法器基本单元_12  (
    .in_2(\n32位除法器基本单元_9_out_5 ), .in_3(in_2), .out_4(\n32位除法器基本单元_12_out_4 ),
    .out_5(\n32位除法器基本单元_12_out_5 ), .in_1(\n32位除法器基本单元_9_out_4 ));
  \_32位除法器基本单元  \u_32位除法器基本单元_13  (
    .in_2(\n32位除法器基本单元_10_out_5 ), .in_3(in_2), .out_4(\n32位除法器基本单元_13_out_4 ),
    .out_5(\n32位除法器基本单元_13_out_5 ), .in_1(\n32位除法器基本单元_10_out_4 ));
  \_32位除法器基本单元  \u_32位除法器基本单元_14  (
    .in_2(\n32位除法器基本单元_11_out_5 ), .in_3(in_2), .out_4(\n32位除法器基本单元_14_out_4 ),
    .out_5(\n32位除法器基本单元_14_out_5 ), .in_1(\n32位除法器基本单元_11_out_4 ));
  \_32位除法器基本单元  \u_32位除法器基本单元_15  (
    .in_2(\n32位除法器基本单元_12_out_5 ), .in_3(in_2), .out_4(\n32位除法器基本单元_15_out_4 ),
    .out_5(\n32位除法器基本单元_15_out_5 ), .in_1(\n32位除法器基本单元_12_out_4 ));
  \_32位除法器基本单元  \u_32位除法器基本单元_16  (
    .in_2(\n32位除法器基本单元_13_out_5 ), .in_3(in_2), .out_4(\n32位除法器基本单元_16_out_4 ),
    .out_5(\n32位除法器基本单元_16_out_5 ), .in_1(\n32位除法器基本单元_13_out_4 ));
  \_32位除法器基本单元  \u_32位除法器基本单元_17  (
    .in_2(\n32位除法器基本单元_14_out_5 ), .in_3(in_2), .out_4(\n32位除法器基本单元_17_out_4 ),
    .out_5(\n32位除法器基本单元_17_out_5 ), .in_1(\n32位除法器基本单元_14_out_4 ));
  \_32位除法器基本单元  \u_32位除法器基本单元_18  (
    .in_2(\n32位除法器基本单元_15_out_5 ), .in_3(in_2), .out_4(\n32位除法器基本单元_18_out_4 ),
    .out_5(\n32位除法器基本单元_18_out_5 ), .in_1(\n32位除法器基本单元_15_out_4 ));
  \_32位除法器基本单元  \u_32位除法器基本单元_19  (
    .in_2(\n32位除法器基本单元_16_out_5 ), .in_3(in_2), .out_4(\n32位除法器基本单元_19_out_4 ),
    .out_5(\n32位除法器基本单元_19_out_5 ), .in_1(\n32位除法器基本单元_16_out_4 ));
  \_32位除法器基本单元  \u_32位除法器基本单元_20  (
    .in_2(\n32位除法器基本单元_18_out_5 ), .in_3(in_2), .out_4(\n32位除法器基本单元_20_out_4 ),
    .out_5(\n32位除法器基本单元_20_out_5 ), .in_1(\n32位除法器基本单元_18_out_4 ));
  \_32位除法器基本单元  \u_32位除法器基本单元_21  (
    .in_2(\n32位除法器基本单元_17_out_5 ), .in_3(in_2), .out_4(\n32位除法器基本单元_21_out_4 ),
    .out_5(\n32位除法器基本单元_21_out_5 ), .in_1(\n32位除法器基本单元_17_out_4 ));
  \_32位除法器基本单元  \u_32位除法器基本单元_22  (
    .in_2(\n32位除法器基本单元_19_out_5 ), .in_3(in_2), .out_4(\n32位除法器基本单元_22_out_4 ),
    .out_5(\n32位除法器基本单元_22_out_5 ), .in_1(\n32位除法器基本单元_19_out_4 ));
  \_32位除法器基本单元  \u_32位除法器基本单元_23  (
    .in_2(\n32位除法器基本单元_20_out_5 ), .in_3(in_2), .out_4(\n32位除法器基本单元_23_out_4 ),
    .out_5(\n32位除法器基本单元_23_out_5 ), .in_1(\n32位除法器基本单元_20_out_4 ));
  \_32位除法器基本单元  \u_32位除法器基本单元_24  (
    .in_2(\n32位除法器基本单元_21_out_5 ), .in_3(in_2), .out_4(\n32位除法器基本单元_24_out_4 ),
    .out_5(\n32位除法器基本单元_24_out_5 ), .in_1(\n32位除法器基本单元_21_out_4 ));
  \_32位除法器基本单元  \u_32位除法器基本单元_25  (
    .in_2(\n32位除法器基本单元_22_out_5 ), .in_3(in_2), .out_4(\n32位除法器基本单元_25_out_4 ),
    .out_5(\n32位除法器基本单元_25_out_5 ), .in_1(\n32位除法器基本单元_22_out_4 ));
  \_32位除法器基本单元  \u_32位除法器基本单元_26  (
    .in_2(\n32位除法器基本单元_24_out_5 ), .in_3(in_2), .out_4(\n32位除法器基本单元_26_out_4 ),
    .out_5(\n32位除法器基本单元_26_out_5 ), .in_1(\n32位除法器基本单元_24_out_4 ));
  \_32位除法器基本单元  \u_32位除法器基本单元_27  (
    .in_2(\n32位除法器基本单元_23_out_5 ), .in_3(in_2), .out_4(\n32位除法器基本单元_27_out_4 ),
    .out_5(\n32位除法器基本单元_27_out_5 ), .in_1(\n32位除法器基本单元_23_out_4 ));
  \_32位除法器基本单元  \u_32位除法器基本单元_28  (
    .in_2(\n32位除法器基本单元_25_out_5 ), .in_3(in_2), .out_4(\n32位除法器基本单元_28_out_4 ),
    .out_5(\n32位除法器基本单元_28_out_5 ), .in_1(\n32位除法器基本单元_25_out_4 ));
  \_32位除法器基本单元  \u_32位除法器基本单元_29  (
    .in_2(\n32位除法器基本单元_26_out_5 ), .in_3(in_2), .out_4(\n32位除法器基本单元_29_out_4 ),
    .out_5(\n32位除法器基本单元_29_out_5 ), .in_1(\n32位除法器基本单元_26_out_4 ));
  \_32位除法器基本单元  \u_32位除法器基本单元_30  (
    .in_2(\n32位除法器基本单元_27_out_5 ), .in_3(in_2), .out_4(out_3), .out_5(out_4), .in_1(\n32位除法器基本单元_27_out_4 ));
  \_32位除法器基本单元  \u_32位除法器基本单元_31  (
    .in_2(\n32位除法器基本单元_28_out_5 ), .in_3(in_2), .out_4(\n32位除法器基本单元_31_out_4 ),
    .out_5(\n32位除法器基本单元_31_out_5 ), .in_1(\n32位除法器基本单元_28_out_4 ));
  \_32位除法器基本单元  \u_32位除法器基本单元_32  (
    .in_2(\n32位除法器基本单元_31_out_5 ), .in_3(in_2), .out_4(\n32位除法器基本单元_32_out_4 ),
    .out_5(\n32位除法器基本单元_32_out_5 ), .in_1(\n32位除法器基本单元_31_out_4 ));
endmodule

module \_32位除法器测试电路  (
  input  [31:0] in_1,
  input  [31:0] in_2,
  output [31:0] out_3,
  output [31:0] out_4,
  output [31:0] out_5,
  output [31:0] out_6
);

  \_32位除法器  \u_32位除法器_1  (.in_1(in_1), .in_2(in_2), .out_4(out_3));  // open: out_3
  Divider #(.width(32)) divider_1 (.a(in_1), .b(in_2), .out(out_5), .rem(out_6));  // open: upper
endmodule

module \四位除法器基本单元  (
  input  [7:0] in_1,
  input  [3:0] in_2,
  output [7:0] out_3
);

  wire comparator_1_eq, comparator_1_gt, or_1_out;
  wire [7:0] shifter_1_out;
  wire [7:4] subtractor_1_out;

  Shifter #(.width(8), .shift("ll")) shifter_1 (.in(in_1), .\dist (3'b001), .out(shifter_1_out));
  Comparator #(.width(4), .mode("unsigned")) comparator_1 (
    .a(shifter_1_out[7:4]), .b(in_2), .gt(comparator_1_gt), .eq(comparator_1_eq));  // open: lt
  Subtractor #(.width(4)) subtractor_1 (.a(shifter_1_out[7:4]), .b(in_2), .out(subtractor_1_out));  // open: bin, bout
  or or_1 (or_1_out, comparator_1_gt, comparator_1_eq);
  Multiplexer #(.select(1), .width(8), .disabled("Z"), .enable("false")) multiplexer_1 (
    .in0(shifter_1_out), .in1({subtractor_1_out, shifter_1_out[3:1], 1'b1}), .out(out_3), .sel(or_1_out));
  // also tied to GND on the sheet: shifter_1_out[0]
endmodule

module \_32位除法器基本单元  (
  input  [31:0] in_1,
  input  [31:0] in_2,
  input  [31:0] in_3,
  output [31:0] out_4,
  output [31:0] out_5
);

  wire comparator_1_eq, comparator_1_gt, or_1_out;
  wire [31:0] \n64位移位器_1_out_4 , \n64位移位器_1_out_5 , subtractor_1_out;

  \_64位移位器  \u_64位移位器_1  (
    .in_1(in_1), .in_2(5'b00001), .in_3(in_2), .out_4(\n64位移位器_1_out_4 ), .out_5(\n64位移位器_1_out_5 ));
  Comparator #(.width(32), .mode("unsigned")) comparator_1 (
    .a(\n64位移位器_1_out_4 ), .b(in_3), .gt(comparator_1_gt), .eq(comparator_1_eq));  // open: lt
  Subtractor #(.width(32)) subtractor_1 (.a(\n64位移位器_1_out_4 ), .b(in_3), .out(subtractor_1_out));  // open: bin, bout
  or or_1 (or_1_out, comparator_1_gt, comparator_1_eq);
  Multiplexer #(.select(1), .width(32), .disabled("Z"), .enable("false")) multiplexer_1 (
    .in0(\n64位移位器_1_out_4 ), .in1(subtractor_1_out), .out(out_4), .sel(or_1_out));
  Multiplexer #(.select(1), .width(32), .disabled("Z"), .enable("false")) multiplexer_2 (
    .in0(\n64位移位器_1_out_5 ), .in1({\n64位移位器_1_out_5 [31:1], 1'b1}), .out(out_5), .sel(or_1_out));
  // also tied to GND on the sheet: \n64位移位器_1_out_5 [0]
endmodule

module \_64位移位器  (
  input  [31:0] in_1,
  input  [4:0] in_2,
  input  [31:0] in_3,
  output [31:0] out_4,
  output [31:0] out_5
);

  wire [4:0] adder_1_out, subtractor_1_out;
  wire [31:0] shifter_1_out, shifter_2_out;

  Subtractor #(.width(5)) subtractor_1 (.a({5{1'b1}}), .b(in_2), .out(subtractor_1_out));  // open: bin, bout
  Adder #(.width(5)) adder_1 (.a(subtractor_1_out), .b(5'b00001), .out(adder_1_out));  // open: cin, cout
  Shifter #(.width(32), .shift("ll")) shifter_1 (.in(in_1), .\dist (in_2), .out(shifter_1_out));
  Shifter #(.width(32), .shift("lr")) shifter_2 (.in(in_3), .\dist (adder_1_out), .out(shifter_2_out));
  Shifter #(.width(32), .shift("ll")) shifter_3 (.in(in_3), .\dist (in_2), .out(out_5));
  Adder #(.width(32)) adder_2 (.a(shifter_1_out), .b(shifter_2_out), .out(out_4));  // open: cin, cout

  // Notes on the sheet:
  //   高32位
  //   低32位
  //   移位后的低32位
  //   移位后的高32位
endmodule
