// Logisim project 实验5-CS1805-U201814629-裴涵.circ as structural Verilog: 16 circuits, main circuit 四位二进制可逆计数器
module \四位二进制可逆计数器  (
  input  CPd,
  input  LD,
  input  A,
  input  B,
  input  C,
  input  CLR,
  input  CPu,
  input  D,
  output QA,
  output QB,
  output QC,
  output QD
);

  wire and_1_out, and_2_out, and_3_out, and_4_out, and_5_out, and_6_out, and_7_out, and_8_out, and_9_out,
       and_10_out, and_11_out, and_12_out, and_13_out, and_14_out, d_ff_1_qn, d_ff_2_qn, d_ff_3_qn,
       d_ff_4_qn, or_1_out, or_2_out, or_3_out, or_4_out, or_5_out, or_6_out, or_7_out, or_8_out;

  or or_1 (or_1_out, CPd, CPu);
  and and_1 (and_1_out, d_ff_1_qn, CPd);
  or or_2 (or_2_out, and_1_out, and_2_out);
  and and_2 (and_2_out, CPu, ~d_ff_1_qn);  // AND_Gate
  and and_3 (and_3_out, d_ff_2_qn, d_ff_1_qn, CPd);
  and and_4 (and_4_out, ~d_ff_2_qn, ~d_ff_1_qn, CPu);  // AND_Gate
  and and_5 (and_5_out, d_ff_3_qn, d_ff_2_qn, d_ff_1_qn, CPd);
  and and_6 (and_6_out, ~d_ff_3_qn, ~d_ff_2_qn, ~d_ff_1_qn, CPu);  // AND_Gate
  or or_3 (or_3_out, and_3_out, and_4_out);
  or or_4 (or_4_out, and_5_out, and_6_out);
  D_Flip_Flop #(.trigger("falling"), .Pre_Clr_Positions("LEGACY"), .NegatePresetClear("false"), .enable("true"), .NewFFLayout("false")) d_ff_1 (
    .clk(or_1_out), .D(d_ff_1_qn), .Q(QA), .Qn(d_ff_1_qn), .preset(and_13_out), .reset(or_7_out));  // open: en
  D_Flip_Flop #(.trigger("falling"), .Pre_Clr_Positions("LEGACY"), .NegatePresetClear("false"), .enable("true"), .NewFFLayout("false")) d_ff_2 (
    .clk(or_2_out), .D(d_ff_2_qn), .Q(QB), .Qn(d_ff_2_qn), .preset(and_7_out), .reset(or_5_out));  // open: en
  or or_5 (or_5_out, and_8_out, CLR);
  D_Flip_Flop #(.trigger("falling"), .Pre_Clr_Positions("LEGACY"), .NegatePresetClear("false"), .enable("true"), .NewFFLayout("false")) d_ff_3 (
    .clk(or_3_out), .D(d_ff_3_qn), .Q(QC), .Qn(d_ff_3_qn), .preset(and_10_out), .reset(or_6_out));  // open: en
  or or_6 (or_6_out, and_9_out, CLR);
  D_Flip_Flop #(.trigger("falling"), .Pre_Clr_Positions("LEGACY"), .NegatePresetClear("false"), .enable("true"), .NewFFLayout("false")) d_ff_4 (
    .clk(or_4_out), .D(d_ff_4_qn), .Q(QD), .Qn(d_ff_4_qn), .preset(and_14_out), .reset(or_8_out));  // open: en
  or or_7 (or_7_out, and_12_out, CLR);
  and and_7 (and_7_out, ~LD, ~CLR, B);  // AND_Gate
  and and_8 (and_8_out, ~B, ~LD);  // AND_Gate
  and and_9 (and_9_out, ~LD, ~C);  // AND_Gate
  and and_10 (and_10_out, ~CLR, ~LD, C);  // AND_Gate
  or or_8 (or_8_out, CLR, and_11_out);
  and and_11 (and_11_out, ~LD, ~D);  // AND_Gate
  and and_12 (and_12_out, ~LD, ~A);  // AND_Gate
  and and_13 (and_13_out, A, ~LD, ~CLR);  // AND_Gate
  and and_14 (and_14_out, ~CLR, ~LD, D);  // AND_Gate
endmodule

module \六十进制计数器  (
  input  Adj,
  input  CPd,
  input  CLr,
  input  CPu,
  output out_5,
  output out_6,
  output out_7,
  output out_8,
  output out_9,
  output out_10,
  output out_11,
  output out_12,
  output out_13
);

  wire and_1_out, and_2_out, and_3_out, and_4_out, and_5_out, and_6_out, and_7_out, nand_1_out, or_1_out,
       or_2_out, or_3_out, or_4_out;

  or or_1 (or_1_out, out_8, out_7, out_6, out_5, or_3_out);
  and and_1 (and_1_out, CPd, Adj, or_1_out);
  or or_2 (or_2_out, and_2_out, CLr);
  or or_3 (or_3_out, out_11, out_10, out_9, out_12);
  and and_2 (and_2_out, ~out_11, out_10, ~out_9, out_12);  // AND_Gate
  and and_3 (and_3_out, out_11, out_10, out_9, out_12);
  \四位二进制可逆计数器  \u_四位二进制可逆计数器_1  (
    .CPd(and_1_out), .CPu(CPu), .QA(out_11), .LD(nand_1_out), .A(1'b1), .QB(out_10), .B(1'b0), .QC(out_9),
    .C(1'b0), .CLR(or_2_out), .QD(out_12), .D(1'b1));
  nand nand_1 (nand_1_out, ~CPd, and_3_out);  // NAND_Gate
  and and_4 (and_4_out, and_3_out, ~and_1_out);  // AND_Gate
  or or_4 (or_4_out, CLr, and_5_out);
  and and_5 (and_5_out, ~out_8, out_7, out_6, ~out_5);  // AND_Gate
  \四位二进制可逆计数器  \u_四位二进制可逆计数器_2  (
    .CPd(and_4_out), .CPu(and_2_out), .QA(out_8), .LD(1'b1), .A(1'b1), .QB(out_7), .B(1'b1), .QC(out_6),
    .C(1'b1), .CLR(or_4_out), .QD(out_5), .D(1'b1));
  and and_6 (and_6_out, out_8, ~out_7, out_6, ~out_5, out_11, ~out_10, ~out_9, out_12);  // AND_Gate
  and and_7 (and_7_out, and_6_out, CPu);
  not not_1 (out_13, and_7_out);
endmodule

module \六十进制计数器测试电路  (
  input  in_1,
  input  in_2,
  output out_3
);

  wire button_1_out, button_2_out;
  wire [3:0] \六十进制计数器_1_out_8 , \六十进制计数器_1_out_11 ;

  Button button_1 (.out(button_1_out));
  Button button_2 (.out(button_2_out));
  Hex_Digit_Display hex_digit_display_1 (.value(\六十进制计数器_1_out_8 ));  // open: dp
  Hex_Digit_Display hex_digit_display_2 (.value(\六十进制计数器_1_out_11 ));  // open: dp
  \六十进制计数器  \u_六十进制计数器_1  (
    .Adj(in_1), .CPd(button_2_out), .CLr(in_2), .CPu(button_1_out), .out_13(out_3),
    .out_12(\六十进制计数器_1_out_11 [3]), .out_9(\六十进制计数器_1_out_11 [2]), .out_10(\六十进制计数器_1_out_11 [1]),
    .out_11(\六十进制计数器_1_out_11 [0]), .out_5(\六十进制计数器_1_out_8 [3]), .out_6(\六十进制计数器_1_out_8 [2]),
    .out_7(\六十进制计数器_1_out_8 [1]), .out_8(\六十进制计数器_1_out_8 [0]));
endmodule

module \十二进制计数器或二十四进制的计数器电路  (
  input  in_1,
  input  in_2,
  input  in_3,
  input  in_4,
  input  in_5,
  output out_6,
  output out_7,
  output out_8,
  output out_9,
  output out_10,
  output out_11,
  output out_12,
  output out_13,
  output out_14
);

  wire and_1_out, and_2_out, and_3_out, \n24转12_1_i , not_1_out, not_2_out, not_3_out, or_1_out,
       \六十进制计数器_1_out_11 ;
  wire [7:0] buffer_1_out, \n24转12_1_h_2 ;

  \六十进制计数器  \u_六十进制计数器_1  (
    .Adj(in_3), .CPd(in_4), .CLr(or_1_out), .CPu(in_2), .out_12(buffer_1_out[3]), .out_9(buffer_1_out[2]),
    .out_10(buffer_1_out[1]), .out_11(\六十进制计数器_1_out_11 ), .out_5(buffer_1_out[7]), .out_6(buffer_1_out[6]),
    .out_7(buffer_1_out[5]), .out_8(buffer_1_out[4]));  // open: out_13
  buf buffer_1 (buffer_1_out[0], \六十进制计数器_1_out_11 );
  and and_1 (and_1_out, ~buffer_1_out[0], buffer_1_out[1], ~buffer_1_out[2], ~buffer_1_out[3], buffer_1_out[4]);  // AND_Gate
  or or_1 (or_1_out, and_2_out, in_5);
  \_24转12  \u_24转12_1  (
    .A(buffer_1_out[7]), .a_2(\n24转12_1_h_2 [7]), .B(buffer_1_out[6]), .b_2(\n24转12_1_h_2 [6]),
    .C(buffer_1_out[5]), .D(buffer_1_out[4]), .E(buffer_1_out[3]), .c_2(\n24转12_1_h_2 [5]),
    .F(buffer_1_out[2]), .G(buffer_1_out[1]), .H(buffer_1_out[0]), .d_2(\n24转12_1_h_2 [4]),
    .e_2(\n24转12_1_h_2 [3]), .f_2(\n24转12_1_h_2 [2]), .g_2(\n24转12_1_h_2 [1]), .h_2(\n24转12_1_h_2 [0]),
    .i(\n24转12_1_i ));
  and and_2 (and_2_out, ~buffer_1_out[0], ~buffer_1_out[1], buffer_1_out[2], ~buffer_1_out[3], ~buffer_1_out[4], buffer_1_out[5]);  // AND_Gate
  Multiplexer #(.select(1), .width(8), .disabled("Z"), .enable("false")) multiplexer_1 (
    .in0(\n24转12_1_h_2 ), .in1(buffer_1_out),
    .out({out_6, out_7, out_8, out_9, out_10, out_11, out_12, out_13}), .sel(in_1));
  not not_1 (not_1_out, and_2_out);
  not not_2 (not_2_out, and_1_out);
  and and_3 (and_3_out, \n24转12_1_h_2 [4], ~\n24转12_1_h_2 [3], ~\n24转12_1_h_2 [2], \n24转12_1_h_2 [1], ~\n24转12_1_h_2 [0]);  // AND_Gate
  not not_3 (not_3_out, and_3_out);
  and and_4 (out_14, ~in_1, \n24转12_1_i );  // AND_Gate
  // AND_Gate and_5 has open pins: in0=not_2_out, in1=not_1_out, out=open
endmodule

module \十二进制计数器或二十四进制的计数器测试电路  (
  input  in_1,
  input  in_2,
  input  in_3,
  output out_4
);

  wire button_1_out, button_2_out;
  wire [3:0] \十二进制计数器或二十四进制的计数器电路_1_out_9 , \十二进制计数器或二十四进制的计数器电路_1_out_13 ;

  Button button_1 (.out(button_1_out));
  Button button_2 (.out(button_2_out));
  Hex_Digit_Display hex_digit_display_1 (.value(\十二进制计数器或二十四进制的计数器电路_1_out_9 ));  // open: dp
  Hex_Digit_Display hex_digit_display_2 (.value(\十二进制计数器或二十四进制的计数器电路_1_out_13 ));  // open: dp
  \十二进制计数器或二十四进制的计数器电路  \u_十二进制计数器或二十四进制的计数器电路_1  (
    .out_14(out_4), .in_5(in_3), .in_2(button_1_out), .in_3(in_1), .in_4(button_2_out), .in_1(in_2),
    .out_6(\十二进制计数器或二十四进制的计数器电路_1_out_9 [3]), .out_7(\十二进制计数器或二十四进制的计数器电路_1_out_9 [2]),
    .out_8(\十二进制计数器或二十四进制的计数器电路_1_out_9 [1]), .out_9(\十二进制计数器或二十四进制的计数器电路_1_out_9 [0]),
    .out_10(\十二进制计数器或二十四进制的计数器电路_1_out_13 [3]), .out_11(\十二进制计数器或二十四进制的计数器电路_1_out_13 [2]),
    .out_12(\十二进制计数器或二十四进制的计数器电路_1_out_13 [1]), .out_13(\十二进制计数器或二十四进制的计数器电路_1_out_13 [0]));
endmodule

module \上下午文字显示的电路  (
  input  AM_TM,
  input  TT,
  output [4:0] out_3,
  output [4:0] out_4,
  output [4:0] out_5,
  output [4:0] out_6
);

  wire [19:0] multiplexer_1_out;

  Multiplexer #(.select(1), .width(20), .disabled("Z"), .enable("false")) multiplexer_1 (
    .in0(20'hfca1), .in1(20'h87e90), .out(multiplexer_1_out), .sel(AM_TM));
  Multiplexer #(.select(1), .width(20), .disabled("Z"), .enable("false")) multiplexer_2 (
    .in0({20{1'b0}}), .in1(multiplexer_1_out), .out({out_6, out_5, out_4, out_3}), .sel(TT));
endmodule

module \上下午文字显示测试电路  (
  input  in_1,
  input  in_2
);

  wire [4:0] \上下午文字显示的电路_1_out_3 , \上下午文字显示的电路_1_out_4 , \上下午文字显示的电路_1_out_5 , \上下午文字显示的电路_1_out_6 ;

  DotMatrix #(.inputtype("column"), .matrixcols(4), .matrixrows(5), .persist(0), .dotshape("square")) dotmatrix_1 (
    .col0(\上下午文字显示的电路_1_out_6 ), .col1(\上下午文字显示的电路_1_out_5 ), .col2(\上下午文字显示的电路_1_out_4 ),
    .col3(\上下午文字显示的电路_1_out_3 ));
  \上下午文字显示的电路  \u_上下午文字显示的电路_1  (
    .out_3(\上下午文字显示的电路_1_out_3 ), .out_4(\上下午文字显示的电路_1_out_4 ), .out_5(\上下午文字显示的电路_1_out_5 ),
    .out_6(\上下午文字显示的电路_1_out_6 ), .AM_TM(in_1), .TT(in_2));
endmodule

module \电子钟整点报时电路  (
  input  in_1,
  input  in_2,
  input  in_3,
  input  in_4,
  input  in_5,
  input  in_6,
  input  in_7,
  input  in_8,
  input  in_9,
  input  in_10,
  input  in_11,
  input  in_12,
  output out_13
);

  wire and_1_out, and_3_out, and_4_out;

  and and_1 (and_1_out, ~in_1, in_2, ~in_3, in_4);  // AND_Gate
  and and_2 (out_13, and_1_out, and_3_out, and_4_out);
  and and_3 (and_3_out, in_5, ~in_6, ~in_7, in_8);  // AND_Gate
  and and_4 (and_4_out, ~in_9, in_10, ~in_11, in_12);  // AND_Gate
endmodule

module \电子钟整点报时电路测试电路  (
  input  set,
  input  Clr,
  input  Adj0,
  input  Adj1
);

  wire and_1_out, and_2_out, and_3_out, and_4_out, and_5_out, and_6_out, button_1_out, button_2_out,
       clock_1_out, multiplexer_1_out, multiplexer_2_out, not_1_out, not_2_out, or_1_out, \六十进制计数器_1_out_13 ,
       \六十进制计数器_2_out_13 , \电子钟整点报时电路_1_out_13 ;
  wire [3:0] \六十进制计数器_1_out_8 , \六十进制计数器_1_out_11 , \六十进制计数器_2_out_8 , \六十进制计数器_2_out_11 ,
       \十二进制计数器或二十四进制的计数器电路_1_out_9 , \十二进制计数器或二十四进制的计数器电路_1_out_13 ;

  Button button_1 (.out(button_1_out));
  Clock #(.highDuration(1), .lowDuration(1)) clock_1 (.out(clock_1_out));
  Button button_2 (.out(button_2_out));
  \六十进制计数器  \u_六十进制计数器_1  (
    .Adj(1'b0), .CPd(1'b0), .CLr(Clr), .CPu(clock_1_out), .out_13(\六十进制计数器_1_out_13 ),
    .out_12(\六十进制计数器_1_out_11 [3]), .out_9(\六十进制计数器_1_out_11 [2]), .out_10(\六十进制计数器_1_out_11 [1]),
    .out_11(\六十进制计数器_1_out_11 [0]), .out_5(\六十进制计数器_1_out_8 [3]), .out_6(\六十进制计数器_1_out_8 [2]),
    .out_7(\六十进制计数器_1_out_8 [1]), .out_8(\六十进制计数器_1_out_8 [0]));
  not not_1 (not_1_out, \六十进制计数器_1_out_13 );
  and and_1 (and_1_out, not_1_out, ~or_1_out);  // AND_Gate
  or or_1 (or_1_out, and_2_out, and_4_out);
  and and_2 (and_2_out, Adj0, Adj1);
  \电子钟整点报时电路  \u_电子钟整点报时电路_1  (
    .out_13(\电子钟整点报时电路_1_out_13 ), .in_1(\六十进制计数器_2_out_8 [3]), .in_2(\六十进制计数器_2_out_8 [2]),
    .in_3(\六十进制计数器_2_out_8 [1]), .in_4(\六十进制计数器_2_out_8 [0]), .in_5(\六十进制计数器_2_out_11 [3]),
    .in_6(\六十进制计数器_2_out_11 [2]), .in_7(\六十进制计数器_2_out_11 [1]), .in_8(\六十进制计数器_2_out_11 [0]),
    .in_9(\六十进制计数器_1_out_8 [3]), .in_10(\六十进制计数器_1_out_8 [2]), .in_11(\六十进制计数器_1_out_8 [1]),
    .in_12(\六十进制计数器_1_out_8 [0]));
  Multiplexer #(.select(1), .width(1), .disabled("Z"), .enable("false")) multiplexer_1 (
    .in0(and_1_out), .in1(button_1_out), .out(multiplexer_1_out), .sel(and_2_out));
  and and_3 (and_3_out, and_2_out, button_2_out);
  and and_4 (and_4_out, Adj0, ~Adj1);  // AND_Gate
  \六十进制计数器  \u_六十进制计数器_2  (
    .Adj(and_2_out), .CPd(and_3_out), .CLr(Clr), .CPu(multiplexer_1_out), .out_13(\六十进制计数器_2_out_13 ),
    .out_12(\六十进制计数器_2_out_11 [3]), .out_9(\六十进制计数器_2_out_11 [2]), .out_10(\六十进制计数器_2_out_11 [1]),
    .out_11(\六十进制计数器_2_out_11 [0]), .out_5(\六十进制计数器_2_out_8 [3]), .out_6(\六十进制计数器_2_out_8 [2]),
    .out_7(\六十进制计数器_2_out_8 [1]), .out_8(\六十进制计数器_2_out_8 [0]));
  LED #(.active("true")) led_1 (.in(\电子钟整点报时电路_1_out_13 ));
  not not_2 (not_2_out, \六十进制计数器_2_out_13 );
  and and_5 (and_5_out, not_2_out, ~or_1_out);  // AND_Gate
  Multiplexer #(.select(1), .width(1), .disabled("Z"), .enable("false")) multiplexer_2 (
    .in0(and_5_out), .in1(button_1_out), .out(multiplexer_2_out), .sel(and_4_out));
  Hex_Digit_Display hex_digit_display_1 (.value(\十二进制计数器或二十四进制的计数器电路_1_out_9 ));  // open: dp
  and and_6 (and_6_out, and_4_out, button_2_out);
  Hex_Digit_Display hex_digit_display_2 (.value(\十二进制计数器或二十四进制的计数器电路_1_out_13 ));  // open: dp
  \十二进制计数器或二十四进制的计数器电路  \u_十二进制计数器或二十四进制的计数器电路_1  (
    .in_5(Clr), .in_2(multiplexer_2_out), .in_3(and_4_out), .in_4(and_6_out), .in_1(set),
    .out_6(\十二进制计数器或二十四进制的计数器电路_1_out_9 [3]), .out_7(\十二进制计数器或二十四进制的计数器电路_1_out_9 [2]),
    .out_8(\十二进制计数器或二十四进制的计数器电路_1_out_9 [1]), .out_9(\十二进制计数器或二十四进制的计数器电路_1_out_9 [0]),
    .out_10(\十二进制计数器或二十四进制的计数器电路_1_out_13 [3]), .out_11(\十二进制计数器或二十四进制的计数器电路_1_out_13 [2]),
    .out_12(\十二进制计数器或二十四进制的计数器电路_1_out_13 [1]), .out_13(\十二进制计数器或二十四进制的计数器电路_1_out_13 [0]));  // open: out_14
  Hex_Digit_Display hex_digit_display_3 (.value(\六十进制计数器_2_out_8 ));  // open: dp
  Hex_Digit_Display hex_digit_display_4 (.value(\六十进制计数器_2_out_11 ));  // open: dp
  Hex_Digit_Display hex_digit_display_5 (.value(\六十进制计数器_1_out_8 ));  // open: dp
  Hex_Digit_Display hex_digit_display_6 (.value(\六十进制计数器_1_out_11 ));  // open: dp

  // Notes on the sheet:
  //   CPu
  //   CPD
endmodule

module \秒脉冲产生电路  (
  input  in_1,
  output out_2
);

  wire \四位二进制可逆计数器_1_qa , \四位二进制可逆计数器_1_qb , \四位二进制可逆计数器_1_qc , \四位二进制可逆计数器_1_qd ;

  and and_1 (out_2, \四位二进制可逆计数器_1_qd , ~\四位二进制可逆计数器_1_qc , ~\四位二进制可逆计数器_1_qb , ~\四位二进制可逆计数器_1_qa );  // AND_Gate
  \四位二进制可逆计数器  \u_四位二进制可逆计数器_1  (
    .CPd(1'b0), .CPu(in_1), .QA(\四位二进制可逆计数器_1_qa ), .LD(1'b1), .A(1'b1), .QB(\四位二进制可逆计数器_1_qb ), .B(1'b1),
    .QC(\四位二进制可逆计数器_1_qc ), .C(1'b1), .CLR(out_2), .QD(\四位二进制可逆计数器_1_qd ), .D(1'b1));
endmodule

module \多功能数字钟  (
  input  CPu,
  input  in_2,
  input  set,
  input  CPD,
  input  Clr,
  input  Adj0,
  input  Adj1,
  output out_8,
  output [3:0] out_9,
  output [4:0] out_10,
  output [3:0] out_11,
  output [3:0] out_12,
  output [3:0] out_13,
  output [3:0] out_14,
  output [3:0] out_15,
  output [4:0] out_16,
  output [4:0] out_17,
  output [4:0] out_18
);

  wire and_1_out, and_2_out, and_3_out, and_4_out, and_5_out, and_6_out, multiplexer_1_out,
       multiplexer_2_out, not_1_out, not_2_out, not_3_out, or_1_out, \六十进制计数器_1_out_13 , \六十进制计数器_2_out_13 ,
       \十二进制计数器或二十四进制的计数器电路_1_out_14 , \秒脉冲产生电路_1_out_2 ;

  \秒脉冲产生电路  \u_秒脉冲产生电路_1  (.in_1(in_2), .out_2(\秒脉冲产生电路_1_out_2 ));
  \六十进制计数器  \u_六十进制计数器_1  (
    .Adj(1'b0), .CPd(1'b0), .CLr(Clr), .CPu(\秒脉冲产生电路_1_out_2 ), .out_13(\六十进制计数器_1_out_13 ),
    .out_12(out_15[3]), .out_9(out_15[2]), .out_10(out_15[1]), .out_11(out_15[0]), .out_5(out_14[3]),
    .out_6(out_14[2]), .out_7(out_14[1]), .out_8(out_14[0]));
  not not_1 (not_1_out, \六十进制计数器_1_out_13 );
  and and_1 (and_1_out, not_1_out, ~or_1_out);  // AND_Gate
  or or_1 (or_1_out, and_2_out, and_4_out);
  and and_2 (and_2_out, Adj0, Adj1);
  \电子钟整点报时电路  \u_电子钟整点报时电路_1  (
    .out_13(out_8), .in_1(out_12[3]), .in_2(out_12[2]), .in_3(out_12[1]), .in_4(out_12[0]), .in_5(out_13[3]),
    .in_6(out_13[2]), .in_7(out_13[1]), .in_8(out_13[0]), .in_9(out_14[3]), .in_10(out_14[2]),
    .in_11(out_14[1]), .in_12(out_14[0]));
  Multiplexer #(.select(1), .width(1), .disabled("Z"), .enable("false")) multiplexer_1 (
    .in0(and_1_out), .in1(CPu), .out(multiplexer_1_out), .sel(and_2_out));
  and and_3 (and_3_out, and_2_out, CPD);
  and and_4 (and_4_out, Adj0, ~Adj1);  // AND_Gate
  \六十进制计数器  \u_六十进制计数器_2  (
    .Adj(and_2_out), .CPd(and_3_out), .CLr(Clr), .CPu(multiplexer_1_out), .out_13(\六十进制计数器_2_out_13 ),
    .out_12(out_13[3]), .out_9(out_13[2]), .out_10(out_13[1]), .out_11(out_13[0]), .out_5(out_12[3]),
    .out_6(out_12[2]), .out_7(out_12[1]), .out_8(out_12[0]));
  not not_2 (not_2_out, \六十进制计数器_2_out_13 );
  and and_5 (and_5_out, not_2_out, ~or_1_out);  // AND_Gate
  Multiplexer #(.select(1), .width(1), .disabled("Z"), .enable("false")) multiplexer_2 (
    .in0(and_5_out), .in1(CPu), .out(multiplexer_2_out), .sel(and_4_out));
  and and_6 (and_6_out, and_4_out, CPD);
  \十二进制计数器或二十四进制的计数器电路  \u_十二进制计数器或二十四进制的计数器电路_1  (
    .out_14(\十二进制计数器或二十四进制的计数器电路_1_out_14 ), .in_5(Clr), .in_2(multiplexer_2_out), .in_3(and_4_out),
    .in_4(and_6_out), .in_1(set), .out_6(out_9[3]), .out_7(out_9[2]), .out_8(out_9[1]), .out_9(out_9[0]),
    .out_10(out_11[3]), .out_11(out_11[2]), .out_12(out_11[1]), .out_13(out_11[0]));
  \上下午文字显示的电路  \u_上下午文字显示的电路_1  (
    .out_3(out_18), .out_4(out_10), .out_5(out_16), .out_6(out_17), .AM_TM(\十二进制计数器或二十四进制的计数器电路_1_out_14 ),
    .TT(not_3_out));
  not not_3 (not_3_out, set);
endmodule

module \多功能数字钟测试电路  (
  input  in_1,
  input  in_2,
  input  in_3,
  input  in_4
);

  wire button_1_out, button_2_out, clock_1_out, \多功能数字钟_1_out_8 ;
  wire [3:0] \多功能数字钟_1_out_9 , \多功能数字钟_1_out_11 , \多功能数字钟_1_out_12 , \多功能数字钟_1_out_13 , \多功能数字钟_1_out_14 ,
       \多功能数字钟_1_out_15 ;
  wire [4:0] \多功能数字钟_1_out_10 , \多功能数字钟_1_out_16 , \多功能数字钟_1_out_17 , \多功能数字钟_1_out_18 ;

  Hex_Digit_Display hex_digit_display_1 (.value(\多功能数字钟_1_out_9 ));  // open: dp
  Hex_Digit_Display hex_digit_display_2 (.value(\多功能数字钟_1_out_11 ));  // open: dp
  DotMatrix #(.inputtype("column"), .matrixcols(4), .matrixrows(5), .persist(0), .dotshape("square")) dotmatrix_1 (
    .col0(\多功能数字钟_1_out_17 ), .col1(\多功能数字钟_1_out_16 ), .col2(\多功能数字钟_1_out_10 ), .col3(\多功能数字钟_1_out_18 ));
  Button button_1 (.out(button_1_out));
  Clock #(.highDuration(1), .lowDuration(1)) clock_1 (.out(clock_1_out));
  Hex_Digit_Display hex_digit_display_3 (.value(\多功能数字钟_1_out_13 ));  // open: dp
  Hex_Digit_Display hex_digit_display_4 (.value(\多功能数字钟_1_out_12 ));  // open: dp
  \多功能数字钟  \u_多功能数字钟_1  (
    .out_17(\多功能数字钟_1_out_17 ), .in_2(clock_1_out), .Clr(in_4), .Adj0(in_1), .Adj1(in_2),
    .out_8(\多功能数字钟_1_out_8 ), .out_18(\多功能数字钟_1_out_18 ), .set(in_3), .out_9(\多功能数字钟_1_out_9 ),
    .out_11(\多功能数字钟_1_out_11 ), .out_12(\多功能数字钟_1_out_12 ), .out_13(\多功能数字钟_1_out_13 ),
    .out_14(\多功能数字钟_1_out_14 ), .out_15(\多功能数字钟_1_out_15 ), .out_16(\多功能数字钟_1_out_16 ),
    .out_10(\多功能数字钟_1_out_10 ), .CPu(button_1_out), .CPD(button_2_out));
  Button button_2 (.out(button_2_out));
  Hex_Digit_Display hex_digit_display_5 (.value(\多功能数字钟_1_out_15 ));  // open: dp
  Hex_Digit_Display hex_digit_display_6 (.value(\多功能数字钟_1_out_14 ));  // open: dp
  LED #(.active("true")) led_1 (.in(\多功能数字钟_1_out_8 ));
endmodule

module \闹钟  (
  input  [3:0] in_1,
  input  [3:0] in_2,
  input  [3:0] in_3,
  input  [3:0] in_4,
  input  Alarm,
  input  Aset,
  input  in_7,
  input  in_8,
  input  in_9,
  input  in_10,
  input  CPu,
  input  in_12,
  input  CPD,
  input  Clr,
  input  Adj0,
  input  Adj1,
  output [3:0] out_17,
  output [3:0] out_18,
  output [3:0] out_19,
  output [3:0] out_20,
  output out_21
);

  wire and_1_out, and_2_out, and_3_out, and_4_out, and_5_out, and_6_out, or_2_out, or_3_out, xor_5_out,
       xor_6_out, xor_7_out, xor_8_out;
  wire [3:0] or_1_out, xor_1_out, xor_2_out, xor_3_out, xor_4_out;

  and and_1 (and_1_out, CPu, and_4_out, Alarm);
  and and_2 (and_2_out, Alarm, CPD);
  and and_3 (and_3_out, Alarm, Clr);
  and and_4 (and_4_out, Adj0, Alarm, Adj1);
  \六十进制计数器  \u_六十进制计数器_1  (
    .Adj(and_4_out), .CPd(and_2_out), .CLr(and_3_out), .CPu(and_1_out), .out_12(out_18[3]),
    .out_9(out_18[2]), .out_10(out_18[1]), .out_11(out_18[0]), .out_5(out_17[3]), .out_6(out_17[2]),
    .out_7(out_17[1]), .out_8(out_17[0]));  // open: out_13
  and and_5 (and_5_out, Adj0, Alarm, ~Adj1);  // AND_Gate
  and and_6 (and_6_out, CPu, and_5_out);
  \十二进制计数器或二十四进制的计数器电路  \u_十二进制计数器或二十四进制的计数器电路_1  (
    .in_5(and_3_out), .in_2(and_6_out), .in_3(and_5_out), .in_4(and_2_out), .in_1(in_12), .out_6(out_19[3]),
    .out_7(out_19[2]), .out_8(out_19[1]), .out_9(out_19[0]), .out_10(out_20[3]), .out_11(out_20[2]),
    .out_12(out_20[1]), .out_13(out_20[0]));  // open: out_14
  assign xor_1_out = out_17 ^ in_1;  // XOR_Gate xor_1, 4 bits wide
  assign xor_2_out = out_18 ^ in_2;  // XOR_Gate xor_2, 4 bits wide
  assign xor_3_out = out_19 ^ in_3;  // XOR_Gate xor_3, 4 bits wide
  assign xor_4_out = out_20 ^ in_4;  // XOR_Gate xor_4, 4 bits wide
  assign or_1_out = xor_1_out | xor_2_out | xor_3_out | xor_4_out;  // OR_Gate or_1, 4 bits wide
  xor xor_5 (xor_5_out, or_1_out[0], 1'b0);
  xor xor_6 (xor_6_out, 1'b0, or_1_out[1]);
  xor xor_7 (xor_7_out, 1'b0, or_1_out[2]);
  xor xor_8 (xor_8_out, 1'b0, or_1_out[3]);
  or or_2 (or_2_out, xor_5_out, xor_6_out, xor_7_out, xor_8_out);
  or or_3 (or_3_out, in_7, in_8, in_9, in_10);
  and and_7 (out_21, ~or_2_out, ~or_3_out, Aset);  // AND_Gate
endmodule

module \闹钟测试  (
  input  in_1,
  input  in_2,
  input  in_3,
  input  in_4,
  input  in_5,
  input  in_6,
  input  in_7,
  input  in_8,
  input  in_9,
  output [3:0] out_10,
  output [3:0] out_11,
  output [3:0] out_12,
  output [3:0] out_13,
  output [3:0] out_14,
  output [3:0] out_15,
  output out_16,
  output [4:0] out_17,
  output [4:0] out_18,
  output [4:0] out_19,
  output [4:0] out_20,
  output out_21
);

  wire and_1_out, and_2_out, and_3_out, and_4_out, and_5_out, and_6_out, and_7_out, and_8_out;
  wire [3:0] \多功能数字钟_1_out_9 , \多功能数字钟_1_out_11 , \多功能数字钟_1_out_12 , \多功能数字钟_1_out_13 , \闹钟_1_out_17 ,
       \闹钟_1_out_18 , \闹钟_1_out_19 , \闹钟_1_out_20 ;

  and and_1 (and_1_out, in_1, in_4);
  and and_2 (and_2_out, in_3, in_1);
  and and_3 (and_3_out, in_5, in_1);
  and and_4 (and_4_out, in_8, in_1);
  and and_5 (and_5_out, in_9, in_1);
  and and_6 (and_6_out, ~in_1, in_6);  // AND_Gate
  \闹钟  \u_闹钟_1  (
    .in_1(\多功能数字钟_1_out_12 ), .in_2(\多功能数字钟_1_out_13 ), .in_3(\多功能数字钟_1_out_9 ), .in_4(\多功能数字钟_1_out_11 ),
    .CPu(and_5_out), .CPD(and_4_out), .Clr(and_3_out), .Adj0(and_1_out), .Adj1(and_2_out), .out_21(out_16),
    .in_12(in_7), .Alarm(in_1), .out_17(\闹钟_1_out_17 ), .out_18(\闹钟_1_out_18 ), .out_19(\闹钟_1_out_19 ),
    .out_20(\闹钟_1_out_20 ), .Aset(in_2), .in_7(out_14[3]), .in_8(out_14[2]), .in_9(out_14[1]),
    .in_10(out_14[0]));
  and and_7 (and_7_out, ~in_1, in_9);  // AND_Gate
  \多功能数字钟  \u_多功能数字钟_1  (
    .out_17(out_20), .in_2(and_6_out), .Clr(in_5), .Adj0(in_4), .Adj1(in_3), .out_8(out_21), .out_18(out_17),
    .set(in_7), .out_9(\多功能数字钟_1_out_9 ), .out_11(\多功能数字钟_1_out_11 ), .out_12(\多功能数字钟_1_out_12 ),
    .out_13(\多功能数字钟_1_out_13 ), .out_14(out_14), .out_15(out_15), .out_16(out_19), .out_10(out_18),
    .CPu(and_7_out), .CPD(and_8_out));
  and and_8 (and_8_out, in_8, ~in_1);  // AND_Gate
  Multiplexer #(.select(1), .width(4), .disabled("Z"), .enable("false")) multiplexer_1 (
    .in0(\多功能数字钟_1_out_9 ), .in1(\闹钟_1_out_19 ), .out(out_10), .sel(in_1));
  Multiplexer #(.select(1), .width(4), .disabled("Z"), .enable("false")) multiplexer_2 (
    .in0(\多功能数字钟_1_out_11 ), .in1(\闹钟_1_out_20 ), .out(out_11), .sel(in_1));
  Multiplexer #(.select(1), .width(4), .disabled("Z"), .enable("false")) multiplexer_3 (
    .in0(\多功能数字钟_1_out_12 ), .in1(\闹钟_1_out_17 ), .out(out_12), .sel(in_1));
  Multiplexer #(.select(1), .width(4), .disabled("Z"), .enable("false")) multiplexer_4 (
    .in0(\多功能数字钟_1_out_13 ), .in1(\闹钟_1_out_18 ), .out(out_13), .sel(in_1));
endmodule

module \带闹钟的多功能数字钟测试电路  (
  input  in_1,
  input  in_2,
  input  in_3,
  input  in_4,
  input  in_5,
  input  in_6
);

  wire button_1_out, button_2_out, clock_1_out, \闹钟测试_1_out_16 , \闹钟测试_1_out_21 ;
  wire [3:0] \闹钟测试_1_out_10 , \闹钟测试_1_out_11 , \闹钟测试_1_out_12 , \闹钟测试_1_out_13 , \闹钟测试_1_out_14 ,
       \闹钟测试_1_out_15 ;
  wire [4:0] \闹钟测试_1_out_17 , \闹钟测试_1_out_18 , \闹钟测试_1_out_19 , \闹钟测试_1_out_20 ;

  Hex_Digit_Display hex_digit_display_1 (.value(\闹钟测试_1_out_10 ));  // open: dp
  Hex_Digit_Display hex_digit_display_2 (.value(\闹钟测试_1_out_11 ));  // open: dp
  DotMatrix #(.inputtype("column"), .matrixcols(4), .matrixrows(5), .persist(0), .dotshape("square")) dotmatrix_1 (
    .col0(\闹钟测试_1_out_20 ), .col1(\闹钟测试_1_out_19 ), .col2(\闹钟测试_1_out_18 ), .col3(\闹钟测试_1_out_17 ));
  Clock #(.highDuration(1), .lowDuration(1)) clock_1 (.out(clock_1_out));
  Hex_Digit_Display hex_digit_display_3 (.value(\闹钟测试_1_out_13 ));  // open: dp
  Hex_Digit_Display hex_digit_display_4 (.value(\闹钟测试_1_out_12 ));  // open: dp
  Button button_1 (.out(button_1_out));
  Button button_2 (.out(button_2_out));
  Hex_Digit_Display hex_digit_display_5 (.value(\闹钟测试_1_out_14 ));  // open: dp
  Hex_Digit_Display hex_digit_display_6 (.value(\闹钟测试_1_out_15 ));  // open: dp
  LED #(.active("true")) led_1 (.in(\闹钟测试_1_out_16 ));
  \闹钟测试  \u_闹钟测试_1  (
    .in_1(in_3), .in_2(in_4), .out_17(\闹钟测试_1_out_17 ), .out_18(\闹钟测试_1_out_18 ), .out_19(\闹钟测试_1_out_19 ),
    .out_20(\闹钟测试_1_out_20 ), .in_6(clock_1_out), .out_21(\闹钟测试_1_out_21 ), .in_3(in_2), .in_4(in_1),
    .out_10(\闹钟测试_1_out_10 ), .out_11(\闹钟测试_1_out_11 ), .out_12(\闹钟测试_1_out_12 ), .out_13(\闹钟测试_1_out_13 ),
    .out_14(\闹钟测试_1_out_14 ), .out_15(\闹钟测试_1_out_15 ), .in_9(button_2_out), .in_8(button_1_out),
    .in_7(in_5), .in_5(in_6), .out_16(\闹钟测试_1_out_16 ));
  LED #(.active("true")) led_2 (.in(\闹钟测试_1_out_21 ));

  // Notes on the sheet:
  //   备注：Alarm为设置闹钟具体数值的开关
  //   Aset为是否启用闹钟的开关
  //   调整方式Adj两个端口的设置同多功能电子钟
endmodule

module \_24转12  (
  input  A,
  input  B,
  input  C,
  input  D,
  input  E,
  input  F,
  input  G,
  input  H,
  output a_2,
  output b_2,
  output c_2,
  output d_2,
  output e_2,
  output f_2,
  output g_2,
  output h_2,
  output i
);

  wire and_1_out, and_2_out, and_3_out, and_4_out, and_5_out, and_6_out, and_7_out, and_8_out, and_9_out,
       and_10_out, and_11_out, and_12_out, and_13_out, and_14_out, and_15_out, and_16_out, and_17_out,
       and_18_out, and_19_out, and_20_out, and_21_out, and_22_out, and_23_out, and_24_out, and_25_out,
       and_26_out, and_27_out, and_28_out, and_29_out, and_30_out, and_31_out, and_32_out, and_33_out,
       and_34_out, and_35_out, and_36_out, and_37_out, and_38_out, and_39_out, and_40_out, and_41_out,
       and_42_out, and_43_out, not_1_out, not_2_out, not_3_out, not_4_out, not_5_out, not_6_out, not_7_out,
       not_8_out, not_9_out, not_10_out, not_11_out, not_12_out, not_13_out, not_14_out, not_15_out,
       not_16_out, not_17_out, not_18_out, not_19_out, not_20_out, not_21_out, not_22_out, not_23_out,
       not_24_out, not_25_out, not_26_out, not_27_out, not_28_out, not_29_out, not_30_out, not_31_out,
       not_32_out, not_33_out, not_34_out, not_35_out, not_36_out, not_37_out, not_38_out, not_39_out,
       not_40_out, not_41_out, not_42_out, not_43_out, not_44_out, not_45_out, not_46_out, not_47_out,
       not_48_out, not_49_out, not_50_out, not_51_out, not_52_out, not_53_out, not_54_out, not_55_out,
       not_56_out;

  and and_1 (and_1_out, C, F, H);
  and and_2 (and_2_out, C, F, G);
  and and_3 (and_3_out, C, E);
  and and_4 (and_4_out, C, D);
  and and_5 (and_5_out, B, C);
  and and_6 (and_6_out, A, C);
  not not_1 (not_1_out, A);
  not not_2 (not_2_out, B);
  not not_3 (not_3_out, C);
  not not_4 (not_4_out, E);
  not not_5 (not_5_out, F);
  not not_6 (not_6_out, G);
  not not_7 (not_7_out, H);
  not not_8 (not_8_out, E);
  not not_9 (not_9_out, F);
  not not_10 (not_10_out, G);
  not not_11 (not_11_out, E);
  not not_12 (not_12_out, F);
  not not_13 (not_13_out, H);
  not not_14 (not_14_out, A);
  not not_15 (not_15_out, B);
  not not_16 (not_16_out, E);
  not not_17 (not_17_out, F);
  not not_18 (not_18_out, A);
  not not_19 (not_19_out, B);
  not not_20 (not_20_out, E);
  not not_21 (not_21_out, G);
  not not_22 (not_22_out, H);
  not not_23 (not_23_out, D);
  not not_24 (not_24_out, A);
  not not_25 (not_25_out, B);
  not not_26 (not_26_out, D);
  not not_27 (not_27_out, F);
  not not_28 (not_28_out, G);
  not not_29 (not_29_out, D);
  not not_30 (not_30_out, A);
  not not_31 (not_31_out, B);
  not not_32 (not_32_out, C);
  not not_33 (not_33_out, G);
  not not_34 (not_34_out, A);
  not not_35 (not_35_out, B);
  not not_36 (not_36_out, C);
  not not_37 (not_37_out, D);
  not not_38 (not_38_out, E);
  not not_39 (not_39_out, F);
  not not_40 (not_40_out, H);
  not not_41 (not_41_out, C);
  not not_42 (not_42_out, D);
  not not_43 (not_43_out, C);
  not not_44 (not_44_out, F);
  not not_45 (not_45_out, H);
  not not_46 (not_46_out, D);
  not not_47 (not_47_out, A);
  not not_48 (not_48_out, B);
  not not_49 (not_49_out, C);
  not not_50 (not_50_out, E);
  not not_51 (not_51_out, G);
  not not_52 (not_52_out, A);
  not not_53 (not_53_out, B);
  not not_54 (not_54_out, C);
  not not_55 (not_55_out, F);
  and and_7 (and_7_out, D, G);
  and and_8 (and_8_out, D, F);
  and and_9 (and_9_out, D, E);
  and and_10 (and_10_out, C, not_56_out);
  not not_56 (not_56_out, F);
  or or_1 (c_2, and_1_out, and_2_out, and_3_out, and_4_out, and_5_out, and_6_out);
  and and_11 (and_11_out, not_1_out, not_2_out, not_3_out, not_4_out, not_5_out, not_6_out, not_7_out);
  and and_12 (and_12_out, D, not_8_out, not_9_out, not_10_out);
  and and_13 (and_13_out, D, not_11_out, not_12_out, not_13_out);
  and and_14 (and_14_out, D, E, G);
  and and_15 (and_15_out, D, E, F);
  and and_16 (and_16_out, not_14_out, not_15_out, C, not_16_out, not_17_out, G);
  and and_17 (and_17_out, not_18_out, not_19_out, C, not_20_out, F, not_21_out, not_22_out);
  and and_18 (and_18_out, C, D);
  and and_19 (and_19_out, B, D);
  and and_20 (and_20_out, A, D);
  and and_21 (and_21_out, not_23_out, E);
  and and_22 (and_22_out, E, G);
  and and_23 (and_23_out, E, F);
  and and_24 (and_24_out, not_24_out, not_25_out, C, not_26_out, not_27_out, not_28_out);
  and and_25 (and_25_out, C, E);
  and and_26 (and_26_out, B, E);
  and and_27 (and_27_out, A, E);
  and and_28 (and_28_out, not_29_out, F);
  and and_29 (and_29_out, F, G);
  and and_30 (and_30_out, not_30_out, not_31_out, not_32_out, D, E, not_33_out);
  and and_31 (and_31_out, C, F);
  and and_32 (and_32_out, B, F);
  and and_33 (and_33_out, A, F);
  and and_34 (and_34_out, not_34_out, not_35_out, not_36_out, not_37_out, not_38_out, not_39_out, not_40_out);
  and and_35 (and_35_out, not_41_out, not_42_out, G);
  and and_36 (and_36_out, not_43_out, not_44_out, G, not_45_out);
  and and_37 (and_37_out, not_46_out, F, G);
  and and_38 (and_38_out, E, G);
  and and_39 (and_39_out, not_47_out, not_48_out, not_49_out, D, not_50_out, F, not_51_out);
  and and_40 (and_40_out, not_52_out, not_53_out, not_54_out, D, E, not_55_out);
  and and_41 (and_41_out, C, D, G);
  and and_42 (and_42_out, B, G);
  and and_43 (and_43_out, A, G);
  or or_2 (i, and_7_out, and_8_out, and_9_out, and_10_out);
  or or_3 (d_2, and_11_out, and_12_out, and_13_out, and_14_out, and_15_out, and_16_out, and_17_out, and_18_out, and_19_out, and_20_out);
  or or_4 (e_2, and_21_out, and_22_out, and_23_out, and_24_out, and_25_out, and_26_out, and_27_out);
  or or_5 (f_2, and_28_out, and_29_out, and_30_out, and_31_out, and_32_out, and_33_out);
  or or_6 (g_2, and_34_out, and_35_out, and_36_out, and_37_out, and_38_out, and_39_out, and_40_out, and_41_out, and_42_out, and_43_out);

  assign a_2 = A;
  assign b_2 = B;
  assign h_2 = H;
endmodule
